// Logisim project TimeTime.circ as structural Verilog: 43 circuits, main circuit main
module main (
  input  DIPSWITCH1_alarm,
  input  DIPSWITCH2_display,
  input  Y1,
  input  Y2,
  input  Y3,
  input  Y4,
  output S1,
  output S2,
  output S3,
  output S4,
  output RESET,
  output X1,
  output X2,
  output X3,
  output X4,
  output DATAREADY,
  output ONOFF,
  output V_alarm,
  output GND_alarm
);

  wire alarm_1_en_buzzer, and_2_out, B1_long_out_2, B1_out, B2_long_out_2, B2_out, countdown_1_en_buzzer,
       longlong_press_1_out_2, longlong_press_2_out_2, not_1_out, not_2_out, not_3_out, not_4_out, not_5_out,
       not_6_out, not_7_out, or_1_out, or_2_out, or_3_out, or_4_out, s_r_ff_1_q, the_imperial_march_1_gnd,
       the_imperial_march_1_v, the_imperial_march_2_gnd, the_imperial_march_2_v, timeset_1_en_set,
       timeset_display_1_x;
  wire [1:0] fsm_1_state;
  wire [4:0] keypad_1_number;
  wire [7:0] digit_8_1_a, digit_8_2_a, digit_8_3_a, digit_8_4_a, digit_8_5_a, digit_8_6_a;
  wire [29:0] affichage_reset_1_out_1, alarm_1_show_alarm, chrono_1_chrono_time, countdown_1_heure,
       multiplexer_1_out, multiplexer_2_out, multiplexer_3_out, multiplexer_4_out, multiplexer_5_out,
       timeset_1_set_time, watch_1_heure;
  wire [47:0] affichage_reverse1_1_out_2, multiplexer_6_out;

  KEYPAD keypad_1 (
    .RESET(RESET), .y1(Y1), .y2(Y2), .y3(Y3), .y4(Y4), .x1(X1), .x2(X2), .x3(X3), .x4(X4),
    .NUMBER(keypad_1_number), .data_ready(DATAREADY));
  Button B1 (.out(B1_out));
  Button B2 (.out(B2_out));
  longlong_press longlong_press_1 (.in_1(B1_out), .out_2(longlong_press_1_out_2));
  longlong_press longlong_press_2 (.in_1(B2_out), .out_2(longlong_press_2_out_2));
  long_press B1_long (.in_1(B1_out), .out_2(B1_long_out_2));
  long_press B2_long (.in_1(B2_out), .out_2(B2_long_out_2));
  and and_1 (RESET, longlong_press_1_out_2, longlong_press_2_out_2);
  or or_1 (or_1_out, RESET, B1_long_out_2, B2_long_out_2);
  or or_2 (or_2_out, RESET, B1_long_out_2);
  or or_3 (or_3_out, RESET, B1_long_out_2, B2_out);
  FSM fsm_1 (.B1_long(B1_long_out_2), .R(RESET), .STATE(fsm_1_state));
  WATCH watch_1 (
    .RESET(RESET), .EN_set(timeset_1_en_set), .STATE(fsm_1_state), .SET_TIME(timeset_1_set_time),
    .HEURE(watch_1_heure));
  TIMESET timeset_1 (
    .NUMBER(keypad_1_number), .data_ready(DATAREADY), .reset(or_1_out), .B2(B2_out),
    .display(timeset_display_1_x), .SET_TIME(timeset_1_set_time), .EN_set(timeset_1_en_set));
  ALARM alarm_1 (
    .RESET(RESET), .ONOFF(DIPSWITCH1_alarm), .HEURE(watch_1_heure), .EN_set(timeset_1_en_set),
    .STATE(fsm_1_state), .SET_TIME(timeset_1_set_time), .EN_BUZZER(alarm_1_en_buzzer),
    .SHOW_ALARM(alarm_1_show_alarm));
  CHRONO chrono_1 (.B(B1_out), .R(or_3_out), .STATE(fsm_1_state), .CHRONO_TIME(chrono_1_chrono_time));
  COUNTDOWN countdown_1 (
    .StartStop(B1_out), .RESET(or_2_out), .EN_set(timeset_1_en_set), .STATE(fsm_1_state),
    .SET_TIME(timeset_1_set_time), .HEURE(countdown_1_heure), .EN_buzzer(countdown_1_en_buzzer));
  TIMESET_display timeset_display_1 (
    .RESET(RESET), .display(timeset_display_1_x), .B1(B1_out), .B2(B2_out), .B2_long(B2_long_out_2),
    .x(timeset_display_1_x));
  Multiplexer #(.enable("false"), .width(30)) multiplexer_1 (
    .in0(watch_1_heure), .in1(timeset_1_set_time), .out(multiplexer_1_out), .sel(timeset_display_1_x));
  Multiplexer #(.enable("false"), .width(30)) multiplexer_2 (
    .in0(alarm_1_show_alarm), .in1(timeset_1_set_time), .out(multiplexer_2_out), .sel(timeset_display_1_x));
  Multiplexer #(.enable("false"), .width(30)) multiplexer_3 (
    .in0(countdown_1_heure), .in1(timeset_1_set_time), .out(multiplexer_3_out), .sel(timeset_display_1_x));
  Multiplexer #(.enable("false"), .select(2), .width(30)) multiplexer_4 (
    .in0(multiplexer_1_out), .in1(multiplexer_2_out), .in2(chrono_1_chrono_time), .in3(multiplexer_3_out),
    .out(multiplexer_4_out), .sel(fsm_1_state));
  affichage_reset affichage_reset_1 (.out_1(affichage_reset_1_out_1));
  Multiplexer #(.enable("false"), .width(30)) multiplexer_5 (
    .in0(multiplexer_4_out), .in1(affichage_reset_1_out_1), .out(multiplexer_5_out), .sel(RESET));
  not not_1 (not_1_out, DIPSWITCH1_alarm);
  and and_2 (and_2_out, alarm_1_en_buzzer, DIPSWITCH1_alarm);
  S_R_Flip_Flop s_r_ff_1 (.Q(s_r_ff_1_q), .reset(or_4_out), .preset(and_2_out));  // open: S, R, clk, Qn
  or or_4 (or_4_out, not_1_out, RESET);
  not not_2 (not_2_out, DIPSWITCH1_alarm);
  not not_3 (not_3_out, 1'b1);
  not not_4 (not_4_out, fsm_1_state[0]);
  and and_3 (S1, not_4_out, not_5_out);
  not not_5 (not_5_out, fsm_1_state[1]);
  and and_4 (S2, fsm_1_state[0], not_6_out);
  not not_6 (not_6_out, fsm_1_state[1]);
  not not_7 (not_7_out, fsm_1_state[0]);
  and and_5 (S3, not_7_out, fsm_1_state[1]);
  and and_6 (S4, fsm_1_state[0], fsm_1_state[1]);
  digit_8 digit_8_1 (
    .X0(multiplexer_5_out[0]), .X1(multiplexer_5_out[1]), .X2(multiplexer_5_out[2]),
    .X3(multiplexer_5_out[3]), .Y(multiplexer_5_out[4]), .a(digit_8_1_a[0]), .b(digit_8_1_a[1]),
    .c(digit_8_1_a[2]), .d(digit_8_1_a[3]), .e(digit_8_1_a[4]), .f(digit_8_1_a[5]), .g(digit_8_1_a[6]),
    .DOT(digit_8_1_a[7]));
  digit_8 digit_8_2 (
    .X0(multiplexer_5_out[5]), .X1(multiplexer_5_out[6]), .X2(multiplexer_5_out[7]),
    .X3(multiplexer_5_out[8]), .Y(multiplexer_5_out[9]), .a(digit_8_2_a[0]), .b(digit_8_2_a[1]),
    .c(digit_8_2_a[2]), .d(digit_8_2_a[3]), .e(digit_8_2_a[4]), .f(digit_8_2_a[5]), .g(digit_8_2_a[6]),
    .DOT(digit_8_2_a[7]));
  digit_8 digit_8_3 (
    .X0(multiplexer_5_out[10]), .X1(multiplexer_5_out[11]), .X2(multiplexer_5_out[12]),
    .X3(multiplexer_5_out[13]), .Y(multiplexer_5_out[14]), .a(digit_8_3_a[0]), .b(digit_8_3_a[1]),
    .c(digit_8_3_a[2]), .d(digit_8_3_a[3]), .e(digit_8_3_a[4]), .f(digit_8_3_a[5]), .g(digit_8_3_a[6]),
    .DOT(digit_8_3_a[7]));
  digit_8 digit_8_4 (
    .X0(multiplexer_5_out[15]), .X1(multiplexer_5_out[16]), .X2(multiplexer_5_out[17]),
    .X3(multiplexer_5_out[18]), .Y(multiplexer_5_out[19]), .a(digit_8_4_a[0]), .b(digit_8_4_a[1]),
    .c(digit_8_4_a[2]), .d(digit_8_4_a[3]), .e(digit_8_4_a[4]), .f(digit_8_4_a[5]), .g(digit_8_4_a[6]),
    .DOT(digit_8_4_a[7]));
  digit_8 digit_8_5 (
    .X0(multiplexer_5_out[20]), .X1(multiplexer_5_out[21]), .X2(multiplexer_5_out[22]),
    .X3(multiplexer_5_out[23]), .Y(multiplexer_5_out[24]), .a(digit_8_5_a[0]), .b(digit_8_5_a[1]),
    .c(digit_8_5_a[2]), .d(digit_8_5_a[3]), .e(digit_8_5_a[4]), .f(digit_8_5_a[5]), .g(digit_8_5_a[6]),
    .DOT(digit_8_5_a[7]));
  digit_8 digit_8_6 (
    .X0(multiplexer_5_out[25]), .X1(multiplexer_5_out[26]), .X2(multiplexer_5_out[27]),
    .X3(multiplexer_5_out[28]), .Y(multiplexer_5_out[29]), .a(digit_8_6_a[0]), .b(digit_8_6_a[1]),
    .c(digit_8_6_a[2]), .d(digit_8_6_a[3]), .e(digit_8_6_a[4]), .f(digit_8_6_a[5]), .g(digit_8_6_a[6]),
    .DOT(digit_8_6_a[7]));
  The_Imperial_March the_imperial_march_1 (
    .ONOFF(DIPSWITCH1_alarm), .EN_buzzer(s_r_ff_1_q), .RESET(not_2_out), .V(the_imperial_march_1_v),
    .GND(the_imperial_march_1_gnd));
  The_Imperial_March the_imperial_march_2 (
    .ONOFF(1'b1), .EN_buzzer(countdown_1_en_buzzer), .RESET(not_3_out), .V(the_imperial_march_2_v),
    .GND(the_imperial_march_2_gnd));
  or or_5 (V_alarm, the_imperial_march_1_v, the_imperial_march_2_v);
  or or_6 (GND_alarm, the_imperial_march_1_gnd, the_imperial_march_2_gnd);
  affichage_reverse1 affichage_reverse1_1 (
    .in_1({digit_8_6_a, digit_8_5_a, digit_8_4_a, digit_8_3_a, digit_8_2_a, digit_8_1_a}),
    .out_2(affichage_reverse1_1_out_2));
  Multiplexer #(.enable("false"), .width(48)) multiplexer_6 (
    .in0({digit_8_6_a, digit_8_5_a, digit_8_4_a, digit_8_3_a, digit_8_2_a, digit_8_1_a}),
    .in1(affichage_reverse1_1_out_2), .out(multiplexer_6_out), .sel(DIPSWITCH2_display));
  _7_Segment_Display u_7_segment_display_1 (
    .g(multiplexer_6_out[6]), .f(multiplexer_6_out[5]), .a(multiplexer_6_out[0]), .b(multiplexer_6_out[1]),
    .e(multiplexer_6_out[4]), .d(multiplexer_6_out[3]), .c(multiplexer_6_out[2]), .dp(multiplexer_6_out[7]));
  _7_Segment_Display u_7_segment_display_2 (
    .g(multiplexer_6_out[14]), .f(multiplexer_6_out[13]), .a(multiplexer_6_out[8]), .b(multiplexer_6_out[9]),
    .e(multiplexer_6_out[12]), .d(multiplexer_6_out[11]), .c(multiplexer_6_out[10]),
    .dp(multiplexer_6_out[15]));
  _7_Segment_Display u_7_segment_display_3 (
    .g(multiplexer_6_out[22]), .f(multiplexer_6_out[21]), .a(multiplexer_6_out[16]),
    .b(multiplexer_6_out[17]), .e(multiplexer_6_out[20]), .d(multiplexer_6_out[19]),
    .c(multiplexer_6_out[18]), .dp(multiplexer_6_out[23]));
  _7_Segment_Display u_7_segment_display_4 (
    .g(multiplexer_6_out[30]), .f(multiplexer_6_out[29]), .a(multiplexer_6_out[24]),
    .b(multiplexer_6_out[25]), .e(multiplexer_6_out[28]), .d(multiplexer_6_out[27]),
    .c(multiplexer_6_out[26]), .dp(multiplexer_6_out[31]));
  _7_Segment_Display u_7_segment_display_5 (
    .g(multiplexer_6_out[38]), .f(multiplexer_6_out[37]), .a(multiplexer_6_out[32]),
    .b(multiplexer_6_out[33]), .e(multiplexer_6_out[36]), .d(multiplexer_6_out[35]),
    .c(multiplexer_6_out[34]), .dp(multiplexer_6_out[39]));
  _7_Segment_Display u_7_segment_display_6 (
    .g(multiplexer_6_out[46]), .f(multiplexer_6_out[45]), .a(multiplexer_6_out[40]),
    .b(multiplexer_6_out[41]), .e(multiplexer_6_out[44]), .d(multiplexer_6_out[43]),
    .c(multiplexer_6_out[42]), .dp(multiplexer_6_out[47]));

  assign ONOFF = DIPSWITCH1_alarm;
endmodule

module FSM (
  input  B1_long,
  input  R,
  output [1:0] STATE
);

  wire fsm_sr_1_r0, fsm_sr_1_r1, fsm_sr_1_s0, fsm_sr_1_s1, or_1_out, or_2_out, s_r_ff_1_q, s_r_ff_2_q;

  FSM_SR fsm_sr_1 (
    .Q1(STATE[1]), .Q0(STATE[0]), .B(B1_long), .S1(fsm_sr_1_s1), .R1(fsm_sr_1_r1), .S0(fsm_sr_1_s0),
    .R0(fsm_sr_1_r0));
  S_R_Flip_Flop s_r_ff_1 (.Q(s_r_ff_1_q), .reset(or_1_out), .preset(fsm_sr_1_s1));  // open: S, R, clk, Qn
  or or_1 (or_1_out, fsm_sr_1_r1, R);
  D_Flip_Flop d_ff_1 (.D(s_r_ff_1_q), .clk(B1_long), .Q(STATE[1]), .reset(R));  // open: Qn, preset
  S_R_Flip_Flop s_r_ff_2 (.Q(s_r_ff_2_q), .reset(fsm_sr_1_r0), .preset(or_2_out));  // open: S, R, clk, Qn
  or or_2 (or_2_out, fsm_sr_1_s0, R);
  D_Flip_Flop d_ff_2 (.D(s_r_ff_2_q), .clk(B1_long), .Q(STATE[0]), .reset(R));  // open: Qn, preset
endmodule

module FSM_SR (
  input  Q1,
  input  Q0,
  input  B,
  output S1,
  output R1,
  output S0,
  output R0
);

  wire and_1_out, and_2_out, and_3_out, and_4_out, not_1_out, not_2_out;

  not not_1 (not_1_out, Q1);
  not not_2 (not_2_out, Q0);
  and and_1 (and_1_out, not_1_out, Q0, B);
  and and_2 (and_2_out, Q1, not_2_out, B);
  and and_3 (and_3_out, not_1_out, not_2_out, B);
  and and_4 (and_4_out, Q1, Q0, B);
  and and_5 (S0, not_2_out, B);
  and and_6 (R0, Q0, B);
  or or_1 (S1, and_1_out, and_2_out);
  or or_2 (R1, and_3_out, and_4_out);
endmodule

module WATCH (
  input  RESET,
  input  EN_set,
  input  [1:0] STATE,
  input  [29:0] SET_TIME,
  output [29:0] HEURE
);

  wire and_1_out, and_2_out, count_3_1_u0, count_3_1_u1, count_6_1_co, count_6_1_u0, count_6_1_u1,
       count_6_1_u2, count_6_2_co, count_6_2_u0, count_6_2_u1, count_6_2_u2, count_10_1_co, count_10_1_u0,
       count_10_1_u1, count_10_1_u2, count_10_1_u3, count_10_2_co, count_10_2_u0, count_10_2_u1,
       count_10_2_u2, count_10_2_u3, count_10_4_1_co, count_10_4_1_u0, count_10_4_1_u1, count_10_4_1_u2,
       count_10_4_1_u3, d_ff_5_q, d_ff_9_q, d_ff_14_q, d_ff_18_q, d_ff_23_q, not_1_out, not_2_out, or_1_out,
       or_2_out, or_3_out, or_4_out, or_5_out, or_6_out, SECONDES_out, watch_set_sr_1_r0, watch_set_sr_1_r1,
       watch_set_sr_1_r2, watch_set_sr_1_r3, watch_set_sr_1_rco, watch_set_sr_1_s0, watch_set_sr_1_s1,
       watch_set_sr_1_s2, watch_set_sr_1_s3, watch_set_sr_1_sco, watch_set_sr_2_r0, watch_set_sr_2_r1,
       watch_set_sr_2_r2, watch_set_sr_2_rco, watch_set_sr_2_s0, watch_set_sr_2_s1, watch_set_sr_2_s2,
       watch_set_sr_2_sco, watch_set_sr_3_r0, watch_set_sr_3_r1, watch_set_sr_3_r2, watch_set_sr_3_r3,
       watch_set_sr_3_rco, watch_set_sr_3_s0, watch_set_sr_3_s1, watch_set_sr_3_s2, watch_set_sr_3_s3,
       watch_set_sr_3_sco, watch_set_sr_4_r0, watch_set_sr_4_r1, watch_set_sr_4_r2, watch_set_sr_4_rco,
       watch_set_sr_4_s0, watch_set_sr_4_s1, watch_set_sr_4_s2, watch_set_sr_4_sco, watch_set_sr_5_r0,
       watch_set_sr_5_r1, watch_set_sr_5_r2, watch_set_sr_5_r3, watch_set_sr_5_rco, watch_set_sr_5_s0,
       watch_set_sr_5_s1, watch_set_sr_5_s2, watch_set_sr_5_s3, watch_set_sr_5_sco, watch_set_sr_6_r0,
       watch_set_sr_6_r1, watch_set_sr_6_s0, watch_set_sr_6_s1;

  not not_1 (not_1_out, STATE[0]);
  not not_2 (not_2_out, STATE[1]);
  and and_1 (and_1_out, not_1_out, not_2_out);
  Clock #(.highDuration(8000), .lowDuration(8000)) SECONDES (.out(SECONDES_out));
  and and_2 (and_2_out, EN_set, and_1_out);
  or or_1 (or_1_out, RESET, and_2_out);
  or or_2 (or_2_out, RESET, and_2_out);
  or or_3 (or_3_out, RESET, and_2_out);
  or or_4 (or_4_out, RESET, and_2_out);
  or or_5 (or_5_out, RESET, and_2_out);
  or or_6 (or_6_out, RESET, and_2_out);
  count_10 count_10_1 (
    .Q3(HEURE[3]), .Q2(HEURE[2]), .Q1(HEURE[1]), .Q0(HEURE[0]), .U3(count_10_1_u3), .U2(count_10_1_u2),
    .U1(count_10_1_u1), .U0(count_10_1_u0), .CO(count_10_1_co));
  WATCH_set_SR watch_set_sr_1 (
    .X0(SET_TIME[0]), .X1(SET_TIME[1]), .X2(SET_TIME[2]), .X3(SET_TIME[3]), .Y(SET_TIME[4]), .RESET(RESET),
    .EN(or_1_out), .S3(watch_set_sr_1_s3), .R3(watch_set_sr_1_r3), .S2(watch_set_sr_1_s2),
    .R2(watch_set_sr_1_r2), .S1(watch_set_sr_1_s1), .R1(watch_set_sr_1_r1), .S0(watch_set_sr_1_s0),
    .R0(watch_set_sr_1_r0), .SCO(watch_set_sr_1_sco), .RCO(watch_set_sr_1_rco));
  count_6 count_6_1 (
    .Q2(HEURE[7]), .Q1(HEURE[6]), .Q0(HEURE[5]), .U2(count_6_1_u2), .U1(count_6_1_u1), .U0(count_6_1_u0),
    .CO(count_6_1_co));
  WATCH_set_SR watch_set_sr_2 (
    .X0(SET_TIME[5]), .X1(SET_TIME[6]), .X2(SET_TIME[7]), .X3(SET_TIME[8]), .Y(SET_TIME[9]), .RESET(RESET),
    .EN(or_2_out), .S2(watch_set_sr_2_s2), .R2(watch_set_sr_2_r2), .S1(watch_set_sr_2_s1),
    .R1(watch_set_sr_2_r1), .S0(watch_set_sr_2_s0), .R0(watch_set_sr_2_r0), .SCO(watch_set_sr_2_sco),
    .RCO(watch_set_sr_2_rco));  // open: S3, R3
  count_10 count_10_2 (
    .Q3(HEURE[13]), .Q2(HEURE[12]), .Q1(HEURE[11]), .Q0(HEURE[10]), .U3(count_10_2_u3), .U2(count_10_2_u2),
    .U1(count_10_2_u1), .U0(count_10_2_u0), .CO(count_10_2_co));
  WATCH_set_SR watch_set_sr_3 (
    .X0(SET_TIME[10]), .X1(SET_TIME[11]), .X2(SET_TIME[12]), .X3(SET_TIME[13]), .Y(SET_TIME[14]),
    .RESET(RESET), .EN(or_3_out), .S3(watch_set_sr_3_s3), .R3(watch_set_sr_3_r3), .S2(watch_set_sr_3_s2),
    .R2(watch_set_sr_3_r2), .S1(watch_set_sr_3_s1), .R1(watch_set_sr_3_r1), .S0(watch_set_sr_3_s0),
    .R0(watch_set_sr_3_r0), .SCO(watch_set_sr_3_sco), .RCO(watch_set_sr_3_rco));
  count_6 count_6_2 (
    .Q2(HEURE[17]), .Q1(HEURE[16]), .Q0(HEURE[15]), .U2(count_6_2_u2), .U1(count_6_2_u1), .U0(count_6_2_u0),
    .CO(count_6_2_co));
  WATCH_set_SR watch_set_sr_4 (
    .X0(SET_TIME[15]), .X1(SET_TIME[16]), .X2(SET_TIME[17]), .X3(SET_TIME[18]), .Y(SET_TIME[19]),
    .RESET(RESET), .EN(or_4_out), .S2(watch_set_sr_4_s2), .R2(watch_set_sr_4_r2), .S1(watch_set_sr_4_s1),
    .R1(watch_set_sr_4_r1), .S0(watch_set_sr_4_s0), .R0(watch_set_sr_4_r0), .SCO(watch_set_sr_4_sco),
    .RCO(watch_set_sr_4_rco));  // open: S3, R3
  count_10_4 count_10_4_1 (
    .H(HEURE[26]), .Q3(HEURE[23]), .Q2(HEURE[22]), .Q1(HEURE[21]), .Q0(HEURE[20]), .U3(count_10_4_1_u3),
    .U2(count_10_4_1_u2), .U1(count_10_4_1_u1), .U0(count_10_4_1_u0), .CO(count_10_4_1_co));
  WATCH_set_SR watch_set_sr_5 (
    .X0(SET_TIME[20]), .X1(SET_TIME[21]), .X2(SET_TIME[22]), .X3(SET_TIME[23]), .Y(SET_TIME[24]),
    .RESET(RESET), .EN(or_5_out), .S3(watch_set_sr_5_s3), .R3(watch_set_sr_5_r3), .S2(watch_set_sr_5_s2),
    .R2(watch_set_sr_5_r2), .S1(watch_set_sr_5_s1), .R1(watch_set_sr_5_r1), .S0(watch_set_sr_5_s0),
    .R0(watch_set_sr_5_r0), .SCO(watch_set_sr_5_sco), .RCO(watch_set_sr_5_rco));
  count_3 count_3_1 (.Q1(HEURE[26]), .Q0(HEURE[25]), .U1(count_3_1_u1), .U0(count_3_1_u0));  // open: CO
  WATCH_set_SR watch_set_sr_6 (
    .X0(SET_TIME[25]), .X1(SET_TIME[26]), .X2(SET_TIME[27]), .X3(SET_TIME[28]), .Y(SET_TIME[29]),
    .RESET(RESET), .EN(or_6_out), .S1(watch_set_sr_6_s1), .R1(watch_set_sr_6_r1), .S0(watch_set_sr_6_s0),
    .R0(watch_set_sr_6_r0));  // open: S3, R3, S2, R2, SCO, RCO
  D_Flip_Flop d_ff_1 (
    .D(count_10_1_u3), .clk(SECONDES_out), .Q(HEURE[3]), .preset(watch_set_sr_1_s3), .reset(watch_set_sr_1_r3));  // open: Qn
  D_Flip_Flop d_ff_2 (
    .D(count_10_1_u2), .clk(SECONDES_out), .Q(HEURE[2]), .preset(watch_set_sr_1_s2), .reset(watch_set_sr_1_r2));  // open: Qn
  D_Flip_Flop d_ff_3 (
    .D(count_10_1_u1), .clk(SECONDES_out), .Q(HEURE[1]), .preset(watch_set_sr_1_s1), .reset(watch_set_sr_1_r1));  // open: Qn
  D_Flip_Flop d_ff_4 (
    .D(count_10_1_u0), .clk(SECONDES_out), .Q(HEURE[0]), .preset(watch_set_sr_1_s0), .reset(watch_set_sr_1_r0));  // open: Qn
  D_Flip_Flop d_ff_5 (
    .D(count_10_1_co), .clk(SECONDES_out), .Q(d_ff_5_q), .preset(watch_set_sr_1_sco),
    .reset(watch_set_sr_1_rco));  // open: Qn
  D_Flip_Flop d_ff_6 (
    .D(count_6_1_u2), .clk(d_ff_5_q), .Q(HEURE[7]), .preset(watch_set_sr_2_s2), .reset(watch_set_sr_2_r2));  // open: Qn
  D_Flip_Flop d_ff_7 (
    .D(count_6_1_u1), .clk(d_ff_5_q), .Q(HEURE[6]), .preset(watch_set_sr_2_s1), .reset(watch_set_sr_2_r1));  // open: Qn
  D_Flip_Flop d_ff_8 (
    .D(count_6_1_u0), .clk(d_ff_5_q), .Q(HEURE[5]), .preset(watch_set_sr_2_s0), .reset(watch_set_sr_2_r0));  // open: Qn
  D_Flip_Flop d_ff_9 (
    .D(count_6_1_co), .clk(d_ff_5_q), .Q(d_ff_9_q), .preset(watch_set_sr_2_sco), .reset(watch_set_sr_2_rco));  // open: Qn
  D_Flip_Flop d_ff_10 (
    .D(count_10_2_u3), .clk(d_ff_9_q), .Q(HEURE[13]), .preset(watch_set_sr_3_s3), .reset(watch_set_sr_3_r3));  // open: Qn
  D_Flip_Flop d_ff_11 (
    .D(count_10_2_u2), .clk(d_ff_9_q), .Q(HEURE[12]), .preset(watch_set_sr_3_s2), .reset(watch_set_sr_3_r2));  // open: Qn
  D_Flip_Flop d_ff_12 (
    .D(count_10_2_u1), .clk(d_ff_9_q), .Q(HEURE[11]), .preset(watch_set_sr_3_s1), .reset(watch_set_sr_3_r1));  // open: Qn
  D_Flip_Flop d_ff_13 (
    .D(count_10_2_u0), .clk(d_ff_9_q), .Q(HEURE[10]), .preset(watch_set_sr_3_s0), .reset(watch_set_sr_3_r0));  // open: Qn
  D_Flip_Flop d_ff_14 (
    .D(count_10_2_co), .clk(d_ff_9_q), .Q(d_ff_14_q), .preset(watch_set_sr_3_sco), .reset(watch_set_sr_3_rco));  // open: Qn
  D_Flip_Flop d_ff_15 (
    .D(count_6_2_u2), .clk(d_ff_14_q), .Q(HEURE[17]), .preset(watch_set_sr_4_s2), .reset(watch_set_sr_4_r2));  // open: Qn
  D_Flip_Flop d_ff_16 (
    .D(count_6_2_u1), .clk(d_ff_14_q), .Q(HEURE[16]), .preset(watch_set_sr_4_s1), .reset(watch_set_sr_4_r1));  // open: Qn
  D_Flip_Flop d_ff_17 (
    .D(count_6_2_u0), .clk(d_ff_14_q), .Q(HEURE[15]), .preset(watch_set_sr_4_s0), .reset(watch_set_sr_4_r0));  // open: Qn
  D_Flip_Flop d_ff_18 (
    .D(count_6_2_co), .clk(d_ff_14_q), .Q(d_ff_18_q), .preset(watch_set_sr_4_sco), .reset(watch_set_sr_4_rco));  // open: Qn
  D_Flip_Flop d_ff_19 (
    .D(count_10_4_1_u3), .clk(d_ff_18_q), .Q(HEURE[23]), .preset(watch_set_sr_5_s3), .reset(watch_set_sr_5_r3));  // open: Qn
  D_Flip_Flop d_ff_20 (
    .D(count_10_4_1_u2), .clk(d_ff_18_q), .Q(HEURE[22]), .preset(watch_set_sr_5_s2), .reset(watch_set_sr_5_r2));  // open: Qn
  D_Flip_Flop d_ff_21 (
    .D(count_10_4_1_u1), .clk(d_ff_18_q), .Q(HEURE[21]), .preset(watch_set_sr_5_s1), .reset(watch_set_sr_5_r1));  // open: Qn
  D_Flip_Flop d_ff_22 (
    .D(count_10_4_1_u0), .clk(d_ff_18_q), .Q(HEURE[20]), .preset(watch_set_sr_5_s0), .reset(watch_set_sr_5_r0));  // open: Qn
  D_Flip_Flop d_ff_23 (
    .D(count_10_4_1_co), .clk(d_ff_18_q), .Q(d_ff_23_q), .preset(watch_set_sr_5_sco),
    .reset(watch_set_sr_5_rco));  // open: Qn
  D_Flip_Flop d_ff_24 (
    .D(count_3_1_u1), .clk(d_ff_23_q), .Q(HEURE[26]), .preset(watch_set_sr_6_s1), .reset(watch_set_sr_6_r1));  // open: Qn
  D_Flip_Flop d_ff_25 (
    .D(count_3_1_u0), .clk(d_ff_23_q), .Q(HEURE[25]), .preset(watch_set_sr_6_s0), .reset(watch_set_sr_6_r0));  // open: Qn

  assign {HEURE[29:27], HEURE[24], HEURE[19:18], HEURE[14], HEURE[9:8], HEURE[4]} = 10'h49;

  // Notes on the sheet:
  //   secondes (unités)
  //   secondes (dizaines)
  //   minutes (unités)
  //   minutes (dizaines)
  //   heures (unités)
  //   heures (dizaines)
endmodule

module WATCH_set_SR (
  input  X0,
  input  X1,
  input  X2,
  input  X3,
  input  Y,
  input  RESET,
  input  EN,
  output S3,
  output R3,
  output S2,
  output R2,
  output S1,
  output R1,
  output S0,
  output R0,
  output SCO,
  output RCO
);

  wire not_1_out, not_2_out, not_3_out, not_4_out, or_1_out, or_2_out, or_3_out, or_4_out;

  not not_1 (not_1_out, X0);
  not not_2 (not_2_out, X1);
  not not_3 (not_3_out, X2);
  not not_4 (not_4_out, X3);
  or or_1 (or_1_out, not_1_out, RESET);
  or or_2 (or_2_out, not_2_out, RESET);
  or or_3 (or_3_out, not_3_out, RESET);
  or or_4 (or_4_out, not_4_out, RESET);
  Multiplexer #(.enable("false")) multiplexer_1 (.in0(1'b0), .in1(X3), .out(S3), .sel(EN));
  Multiplexer #(.enable("false")) multiplexer_2 (.in0(1'b0), .in1(or_4_out), .out(R3), .sel(EN));
  Multiplexer #(.enable("false")) multiplexer_3 (.in0(1'b0), .in1(X2), .out(S2), .sel(EN));
  Multiplexer #(.enable("false")) multiplexer_4 (.in0(1'b0), .in1(or_3_out), .out(R2), .sel(EN));
  Multiplexer #(.enable("false")) multiplexer_5 (.in0(1'b0), .in1(X1), .out(S1), .sel(EN));
  Multiplexer #(.enable("false")) multiplexer_6 (.in0(1'b0), .in1(or_2_out), .out(R1), .sel(EN));
  Multiplexer #(.enable("false")) multiplexer_7 (.in0(1'b0), .in1(X0), .out(S0), .sel(EN));
  Multiplexer #(.enable("false")) multiplexer_8 (.in0(1'b0), .in1(or_1_out), .out(R0), .sel(EN));
  Multiplexer #(.enable("false")) multiplexer_9 (.in0(1'b0), .in1(RESET), .out(RCO), .sel(EN));

  assign SCO = 1'b0;
endmodule

module ALARM (
  input  RESET,
  input  ONOFF,
  input  [29:0] HEURE,
  input  EN_set,
  input  [1:0] STATE,
  input  [29:0] SET_TIME,
  output EN_BUZZER,
  output [29:0] SHOW_ALARM
);

  wire alarm_compare_1_en_buzzer, and_1_out, and_2_out, not_1_out;

  not not_1 (not_1_out, STATE[1]);
  and and_1 (and_1_out, STATE[0], not_1_out);
  and and_2 (and_2_out, EN_set, and_1_out);
  ALARM_register alarm_register_1 (.RESET(RESET), .EN_set(and_2_out), .SET_TIME(SET_TIME), .ALARM(SHOW_ALARM));
  ALARM_compare alarm_compare_1 (.HEURE(HEURE), .SET_TIME(SHOW_ALARM), .EN_BUZZER(alarm_compare_1_en_buzzer));
  Multiplexer #(.enable("false")) multiplexer_1 (
    .in0(1'b0), .in1(alarm_compare_1_en_buzzer), .out(EN_BUZZER), .sel(ONOFF));
endmodule

module ALARM_compare (
  input  [29:0] HEURE,
  input  [29:0] SET_TIME,
  output EN_BUZZER
);

  wire comparator_1_eq, comparator_2_eq, comparator_3_eq, comparator_4_eq, comparator_5_eq, comparator_6_eq;

  Comparator #(.width(4)) comparator_1 (.a(HEURE[3:0]), .b(SET_TIME[3:0]), .eq(comparator_1_eq));  // open: gt, lt
  Comparator #(.width(4)) comparator_2 (.a(HEURE[8:5]), .b(SET_TIME[8:5]), .eq(comparator_2_eq));  // open: gt, lt
  Comparator #(.width(4)) comparator_3 (.a(HEURE[13:10]), .b(SET_TIME[13:10]), .eq(comparator_3_eq));  // open: gt, lt
  Comparator #(.width(4)) comparator_4 (.a(HEURE[18:15]), .b(SET_TIME[18:15]), .eq(comparator_4_eq));  // open: gt, lt
  Comparator #(.width(4)) comparator_5 (.a(HEURE[23:20]), .b(SET_TIME[23:20]), .eq(comparator_5_eq));  // open: gt, lt
  Comparator #(.width(4)) comparator_6 (.a(HEURE[28:25]), .b(SET_TIME[28:25]), .eq(comparator_6_eq));  // open: gt, lt
  and and_1 (EN_BUZZER, comparator_1_eq, comparator_2_eq, comparator_3_eq, comparator_4_eq, comparator_5_eq, comparator_6_eq);
endmodule

module ALARM_register (
  input  RESET,
  input  EN_set,
  input  [29:0] SET_TIME,
  output [29:0] ALARM
);

  D_Flip_Flop d_ff_1 (.D(SET_TIME[0]), .clk(EN_set), .Q(ALARM[0]), .reset(RESET));  // open: Qn, preset
  D_Flip_Flop d_ff_2 (.D(SET_TIME[1]), .clk(EN_set), .Q(ALARM[1]), .reset(RESET));  // open: Qn, preset
  D_Flip_Flop d_ff_3 (.D(SET_TIME[2]), .clk(EN_set), .Q(ALARM[2]), .reset(RESET));  // open: Qn, preset
  D_Flip_Flop d_ff_4 (.D(SET_TIME[3]), .clk(EN_set), .Q(ALARM[3]), .reset(RESET));  // open: Qn, preset
  D_Flip_Flop d_ff_5 (.D(SET_TIME[5]), .clk(EN_set), .Q(ALARM[5]), .reset(RESET));  // open: Qn, preset
  D_Flip_Flop d_ff_6 (.D(SET_TIME[6]), .clk(EN_set), .Q(ALARM[6]), .reset(RESET));  // open: Qn, preset
  D_Flip_Flop d_ff_7 (.D(SET_TIME[7]), .clk(EN_set), .Q(ALARM[7]), .reset(RESET));  // open: Qn, preset
  D_Flip_Flop d_ff_8 (.D(SET_TIME[8]), .clk(EN_set), .Q(ALARM[8]), .reset(RESET));  // open: Qn, preset
  D_Flip_Flop d_ff_9 (.D(SET_TIME[10]), .clk(EN_set), .Q(ALARM[10]), .reset(RESET));  // open: Qn, preset
  D_Flip_Flop d_ff_10 (.D(SET_TIME[11]), .clk(EN_set), .Q(ALARM[11]), .reset(RESET));  // open: Qn, preset
  D_Flip_Flop d_ff_11 (.D(SET_TIME[12]), .clk(EN_set), .Q(ALARM[12]), .reset(RESET));  // open: Qn, preset
  D_Flip_Flop d_ff_12 (.D(SET_TIME[13]), .clk(EN_set), .Q(ALARM[13]), .reset(RESET));  // open: Qn, preset
  D_Flip_Flop d_ff_13 (.D(SET_TIME[15]), .clk(EN_set), .Q(ALARM[15]), .reset(RESET));  // open: Qn, preset
  D_Flip_Flop d_ff_14 (.D(SET_TIME[16]), .clk(EN_set), .Q(ALARM[16]), .reset(RESET));  // open: Qn, preset
  D_Flip_Flop d_ff_15 (.D(SET_TIME[17]), .clk(EN_set), .Q(ALARM[17]), .reset(RESET));  // open: Qn, preset
  D_Flip_Flop d_ff_16 (.D(SET_TIME[18]), .clk(EN_set), .Q(ALARM[18]), .reset(RESET));  // open: Qn, preset
  D_Flip_Flop d_ff_17 (.D(SET_TIME[20]), .clk(EN_set), .Q(ALARM[20]), .reset(RESET));  // open: Qn, preset
  D_Flip_Flop d_ff_18 (.D(SET_TIME[21]), .clk(EN_set), .Q(ALARM[21]), .reset(RESET));  // open: Qn, preset
  D_Flip_Flop d_ff_19 (.D(SET_TIME[22]), .clk(EN_set), .Q(ALARM[22]), .reset(RESET));  // open: Qn, preset
  D_Flip_Flop d_ff_20 (.D(SET_TIME[23]), .clk(EN_set), .Q(ALARM[23]), .reset(RESET));  // open: Qn, preset
  D_Flip_Flop d_ff_21 (.D(SET_TIME[25]), .clk(EN_set), .Q(ALARM[25]), .reset(RESET));  // open: Qn, preset
  D_Flip_Flop d_ff_22 (.D(SET_TIME[26]), .clk(EN_set), .Q(ALARM[26]), .reset(RESET));  // open: Qn, preset
  D_Flip_Flop d_ff_23 (.D(SET_TIME[27]), .clk(EN_set), .Q(ALARM[27]), .reset(RESET));  // open: Qn, preset
  D_Flip_Flop d_ff_24 (.D(SET_TIME[28]), .clk(EN_set), .Q(ALARM[28]), .reset(RESET));  // open: Qn, preset

  assign {ALARM[29], ALARM[24], ALARM[19], ALARM[14], ALARM[9], ALARM[4]} = 6'b010101;
endmodule

module CHRONO (
  input  B,
  input  R,
  input  [1:0] STATE,
  output [29:0] CHRONO_TIME
);

  wire and_1_out, and_2_out, centi_sec_out, chrono_start_stop_1_q, count_6_1_co, count_6_1_u0, count_6_1_u1,
       count_6_1_u2, count_6_2_u0, count_6_2_u1, count_6_2_u2, count_10_1_co, count_10_1_u0, count_10_1_u1,
       count_10_1_u2, count_10_1_u3, count_10_2_co, count_10_2_u0, count_10_2_u1, count_10_2_u2,
       count_10_2_u3, count_10_3_co, count_10_3_u0, count_10_3_u1, count_10_3_u2, count_10_3_u3,
       count_10_4_co, count_10_4_u0, count_10_4_u1, count_10_4_u2, count_10_4_u3, d_ff_5_q, d_ff_10_q,
       d_ff_15_q, d_ff_19_q, d_ff_24_q, multiplexer_1_out, not_1_out;

  not not_1 (not_1_out, STATE[0]);
  Clock #(.highDuration(80), .lowDuration(80)) centi_sec (.out(centi_sec_out));
  and and_1 (and_1_out, not_1_out, STATE[1]);
  Multiplexer #(.enable("false")) multiplexer_1 (
    .in0(1'b0), .in1(centi_sec_out), .out(multiplexer_1_out), .sel(chrono_start_stop_1_q));
  and and_2 (and_2_out, B, and_1_out);
  CHRONO_start_stop chrono_start_stop_1 (.Q0(chrono_start_stop_1_q), .R(R), .B(and_2_out), .Q(chrono_start_stop_1_q));
  count_10 count_10_1 (
    .Q3(CHRONO_TIME[3]), .Q2(CHRONO_TIME[2]), .Q1(CHRONO_TIME[1]), .Q0(CHRONO_TIME[0]), .U3(count_10_1_u3),
    .U2(count_10_1_u2), .U1(count_10_1_u1), .U0(count_10_1_u0), .CO(count_10_1_co));
  count_10 count_10_2 (
    .Q3(CHRONO_TIME[8]), .Q2(CHRONO_TIME[7]), .Q1(CHRONO_TIME[6]), .Q0(CHRONO_TIME[5]), .U3(count_10_2_u3),
    .U2(count_10_2_u2), .U1(count_10_2_u1), .U0(count_10_2_u0), .CO(count_10_2_co));
  count_10 count_10_3 (
    .Q3(CHRONO_TIME[13]), .Q2(CHRONO_TIME[12]), .Q1(CHRONO_TIME[11]), .Q0(CHRONO_TIME[10]),
    .U3(count_10_3_u3), .U2(count_10_3_u2), .U1(count_10_3_u1), .U0(count_10_3_u0), .CO(count_10_3_co));
  count_6 count_6_1 (
    .Q2(CHRONO_TIME[17]), .Q1(CHRONO_TIME[16]), .Q0(CHRONO_TIME[15]), .U2(count_6_1_u2), .U1(count_6_1_u1),
    .U0(count_6_1_u0), .CO(count_6_1_co));
  count_10 count_10_4 (
    .Q3(CHRONO_TIME[23]), .Q2(CHRONO_TIME[22]), .Q1(CHRONO_TIME[21]), .Q0(CHRONO_TIME[20]),
    .U3(count_10_4_u3), .U2(count_10_4_u2), .U1(count_10_4_u1), .U0(count_10_4_u0), .CO(count_10_4_co));
  count_6 count_6_2 (
    .Q2(CHRONO_TIME[27]), .Q1(CHRONO_TIME[26]), .Q0(CHRONO_TIME[25]), .U2(count_6_2_u2), .U1(count_6_2_u1),
    .U0(count_6_2_u0));  // open: CO
  D_Flip_Flop d_ff_1 (.D(count_10_1_u3), .clk(multiplexer_1_out), .Q(CHRONO_TIME[3]), .reset(R));  // open: Qn, preset
  D_Flip_Flop d_ff_2 (.D(count_10_1_u2), .clk(multiplexer_1_out), .Q(CHRONO_TIME[2]), .reset(R));  // open: Qn, preset
  D_Flip_Flop d_ff_3 (.D(count_10_1_u1), .clk(multiplexer_1_out), .Q(CHRONO_TIME[1]), .reset(R));  // open: Qn, preset
  D_Flip_Flop d_ff_4 (.D(count_10_1_u0), .clk(multiplexer_1_out), .Q(CHRONO_TIME[0]), .reset(R));  // open: Qn, preset
  D_Flip_Flop d_ff_5 (.D(count_10_1_co), .clk(multiplexer_1_out), .Q(d_ff_5_q), .reset(R));  // open: Qn, preset
  D_Flip_Flop d_ff_6 (.D(count_10_2_u3), .clk(d_ff_5_q), .Q(CHRONO_TIME[8]), .reset(R));  // open: Qn, preset
  D_Flip_Flop d_ff_7 (.D(count_10_2_u2), .clk(d_ff_5_q), .Q(CHRONO_TIME[7]), .reset(R));  // open: Qn, preset
  D_Flip_Flop d_ff_8 (.D(count_10_2_u1), .clk(d_ff_5_q), .Q(CHRONO_TIME[6]), .reset(R));  // open: Qn, preset
  D_Flip_Flop d_ff_9 (.D(count_10_2_u0), .clk(d_ff_5_q), .Q(CHRONO_TIME[5]), .reset(R));  // open: Qn, preset
  D_Flip_Flop d_ff_10 (.D(count_10_2_co), .clk(d_ff_5_q), .Q(d_ff_10_q), .reset(R));  // open: Qn, preset
  D_Flip_Flop d_ff_11 (.D(count_10_3_u3), .clk(d_ff_10_q), .Q(CHRONO_TIME[13]), .reset(R));  // open: Qn, preset
  D_Flip_Flop d_ff_12 (.D(count_10_3_u2), .clk(d_ff_10_q), .Q(CHRONO_TIME[12]), .reset(R));  // open: Qn, preset
  D_Flip_Flop d_ff_13 (.D(count_10_3_u1), .clk(d_ff_10_q), .Q(CHRONO_TIME[11]), .reset(R));  // open: Qn, preset
  D_Flip_Flop d_ff_14 (.D(count_10_3_u0), .clk(d_ff_10_q), .Q(CHRONO_TIME[10]), .reset(R));  // open: Qn, preset
  D_Flip_Flop d_ff_15 (.D(count_10_3_co), .clk(d_ff_10_q), .Q(d_ff_15_q), .reset(R));  // open: Qn, preset
  D_Flip_Flop d_ff_16 (.D(count_6_1_u2), .clk(d_ff_15_q), .Q(CHRONO_TIME[17]), .reset(R));  // open: Qn, preset
  D_Flip_Flop d_ff_17 (.D(count_6_1_u1), .clk(d_ff_15_q), .Q(CHRONO_TIME[16]), .reset(R));  // open: Qn, preset
  D_Flip_Flop d_ff_18 (.D(count_6_1_u0), .clk(d_ff_15_q), .Q(CHRONO_TIME[15]), .reset(R));  // open: Qn, preset
  D_Flip_Flop d_ff_19 (.D(count_6_1_co), .clk(d_ff_15_q), .Q(d_ff_19_q), .reset(R));  // open: Qn, preset
  D_Flip_Flop d_ff_20 (.D(count_10_4_u3), .clk(d_ff_19_q), .Q(CHRONO_TIME[23]), .reset(R));  // open: Qn, preset
  D_Flip_Flop d_ff_21 (.D(count_10_4_u2), .clk(d_ff_19_q), .Q(CHRONO_TIME[22]), .reset(R));  // open: Qn, preset
  D_Flip_Flop d_ff_22 (.D(count_10_4_u1), .clk(d_ff_19_q), .Q(CHRONO_TIME[21]), .reset(R));  // open: Qn, preset
  D_Flip_Flop d_ff_23 (.D(count_10_4_u0), .clk(d_ff_19_q), .Q(CHRONO_TIME[20]), .reset(R));  // open: Qn, preset
  D_Flip_Flop d_ff_24 (.D(count_10_4_co), .clk(d_ff_19_q), .Q(d_ff_24_q), .reset(R));  // open: Qn, preset
  D_Flip_Flop d_ff_25 (.D(count_6_2_u2), .clk(d_ff_24_q), .Q(CHRONO_TIME[27]), .reset(R));  // open: Qn, preset
  D_Flip_Flop d_ff_26 (.D(count_6_2_u1), .clk(d_ff_24_q), .Q(CHRONO_TIME[26]), .reset(R));  // open: Qn, preset
  D_Flip_Flop d_ff_27 (.D(count_6_2_u0), .clk(d_ff_24_q), .Q(CHRONO_TIME[25]), .reset(R));  // open: Qn, preset

  assign {CHRONO_TIME[29:28], CHRONO_TIME[24], CHRONO_TIME[19:18], CHRONO_TIME[14], CHRONO_TIME[9], CHRONO_TIME[4]} = 8'h25;

  // Notes on the sheet:
  //   dixièmes (unités)
  //   dixièmes (dizaines)
  //   secondes (unités)
  //   secondes (dizaines)
  //   minutes (unités)
  //   munites (dizaines)
endmodule

module CHRONO_start_stop (
  input  Q0,
  input  R,
  input  B,
  output Q
);

  wire and_1_out, and_2_out, and_3_out, and_4_out, not_1_out, not_2_out, or_1_out, or_2_out, or_3_out,
       s_r_ff_1_q;

  not not_1 (not_1_out, Q0);
  not not_2 (not_2_out, R);
  and and_1 (and_1_out, not_1_out, not_2_out, B);
  and and_2 (and_2_out, Q0, B);
  and and_3 (and_3_out, Q0, R);
  or or_1 (or_1_out, B, R);
  or or_2 (or_2_out, R, and_1_out);
  S_R_Flip_Flop s_r_ff_1 (.Q(s_r_ff_1_q), .reset(or_3_out), .preset(or_2_out));  // open: S, R, clk, Qn
  or or_3 (or_3_out, and_2_out, and_3_out);
  D_Flip_Flop d_ff_1 (.D(s_r_ff_1_q), .clk(or_1_out), .Q(Q), .reset(and_4_out));  // open: Qn, preset
  and and_4 (and_4_out, s_r_ff_1_q, R);
endmodule

module COUNTDOWN (
  input  StartStop,
  input  RESET,
  input  EN_set,
  input  [1:0] STATE,
  input  [29:0] SET_TIME,
  output [29:0] HEURE,
  output EN_buzzer
);

  wire alarm_compare_1_en_buzzer, and_1_out, and_2_out, and_3_out, and_4_out, chrono_start_stop_1_q,
       count_rev_3_1_u0, count_rev_3_1_u1, count_rev_6_1_co, count_rev_6_1_u0, count_rev_6_1_u1,
       count_rev_6_1_u2, count_rev_6_2_co, count_rev_6_2_u0, count_rev_6_2_u1, count_rev_6_2_u2,
       count_rev_10_1_co, count_rev_10_1_u0, count_rev_10_1_u1, count_rev_10_1_u2, count_rev_10_1_u3,
       count_rev_10_2_co, count_rev_10_2_u0, count_rev_10_2_u1, count_rev_10_2_u2, count_rev_10_2_u3,
       count_rev_10_4_1_co, count_rev_10_4_1_u0, count_rev_10_4_1_u1, count_rev_10_4_1_u2,
       count_rev_10_4_1_u3, d_ff_5_q, d_ff_9_q, d_ff_14_q, d_ff_18_q, d_ff_23_q, multiplexer_1_out,
       multiplexer_2_out, not_1_out, not_2_out, not_3_out, or_1_out, or_2_out, or_3_out, or_4_out, or_5_out,
       or_6_out, or_7_out, s_r_ff_1_q, SECONDES_out, watch_set_sr_1_r0, watch_set_sr_1_r1, watch_set_sr_1_r2,
       watch_set_sr_1_r3, watch_set_sr_1_rco, watch_set_sr_1_s0, watch_set_sr_1_s1, watch_set_sr_1_s2,
       watch_set_sr_1_s3, watch_set_sr_1_sco, watch_set_sr_2_r0, watch_set_sr_2_r1, watch_set_sr_2_r2,
       watch_set_sr_2_rco, watch_set_sr_2_s0, watch_set_sr_2_s1, watch_set_sr_2_s2, watch_set_sr_2_sco,
       watch_set_sr_3_r0, watch_set_sr_3_r1, watch_set_sr_3_r2, watch_set_sr_3_r3, watch_set_sr_3_rco,
       watch_set_sr_3_s0, watch_set_sr_3_s1, watch_set_sr_3_s2, watch_set_sr_3_s3, watch_set_sr_3_sco,
       watch_set_sr_4_r0, watch_set_sr_4_r1, watch_set_sr_4_r2, watch_set_sr_4_rco, watch_set_sr_4_s0,
       watch_set_sr_4_s1, watch_set_sr_4_s2, watch_set_sr_4_sco, watch_set_sr_5_r0, watch_set_sr_5_r1,
       watch_set_sr_5_r2, watch_set_sr_5_r3, watch_set_sr_5_rco, watch_set_sr_5_s0, watch_set_sr_5_s1,
       watch_set_sr_5_s2, watch_set_sr_5_s3, watch_set_sr_5_sco, watch_set_sr_6_r0, watch_set_sr_6_r1,
       watch_set_sr_6_s0, watch_set_sr_6_s1;

  Clock #(.highDuration(8000), .lowDuration(8000)) SECONDES (.out(SECONDES_out));
  and and_1 (and_1_out, StartStop, and_2_out, not_1_out);
  not not_1 (not_1_out, alarm_compare_1_en_buzzer);
  and and_2 (and_2_out, STATE[0], STATE[1]);
  and and_3 (and_3_out, EN_set, and_2_out);
  Multiplexer #(.enable("false")) multiplexer_1 (
    .in0(1'b0), .in1(SECONDES_out), .out(multiplexer_1_out), .sel(chrono_start_stop_1_q));
  not not_2 (not_2_out, alarm_compare_1_en_buzzer);
  Multiplexer #(.enable("false")) multiplexer_2 (
    .in0(1'b0), .in1(multiplexer_1_out), .out(multiplexer_2_out), .sel(not_2_out));
  CHRONO_start_stop chrono_start_stop_1 (
    .Q0(chrono_start_stop_1_q), .R(RESET), .B(and_1_out), .Q(chrono_start_stop_1_q));
  or or_1 (or_1_out, RESET, and_3_out);
  or or_2 (or_2_out, RESET, and_3_out);
  or or_3 (or_3_out, RESET, and_3_out);
  or or_4 (or_4_out, RESET, and_3_out);
  or or_5 (or_5_out, RESET, and_3_out);
  or or_6 (or_6_out, RESET, and_3_out);
  count_rev_10 count_rev_10_1 (
    .Q3(HEURE[3]), .Q2(HEURE[2]), .Q1(HEURE[1]), .Q0(HEURE[0]), .U3(count_rev_10_1_u3),
    .U2(count_rev_10_1_u2), .U1(count_rev_10_1_u1), .U0(count_rev_10_1_u0), .CO(count_rev_10_1_co));
  WATCH_set_SR watch_set_sr_1 (
    .X0(SET_TIME[0]), .X1(SET_TIME[1]), .X2(SET_TIME[2]), .X3(SET_TIME[3]), .Y(SET_TIME[4]), .RESET(RESET),
    .EN(or_1_out), .S3(watch_set_sr_1_s3), .R3(watch_set_sr_1_r3), .S2(watch_set_sr_1_s2),
    .R2(watch_set_sr_1_r2), .S1(watch_set_sr_1_s1), .R1(watch_set_sr_1_r1), .S0(watch_set_sr_1_s0),
    .R0(watch_set_sr_1_r0), .SCO(watch_set_sr_1_sco), .RCO(watch_set_sr_1_rco));
  count_rev_6 count_rev_6_1 (
    .Q2(HEURE[7]), .Q1(HEURE[6]), .Q0(HEURE[5]), .U2(count_rev_6_1_u2), .U1(count_rev_6_1_u1),
    .U0(count_rev_6_1_u0), .CO(count_rev_6_1_co));
  WATCH_set_SR watch_set_sr_2 (
    .X0(SET_TIME[5]), .X1(SET_TIME[6]), .X2(SET_TIME[7]), .X3(SET_TIME[8]), .Y(SET_TIME[9]), .RESET(RESET),
    .EN(or_2_out), .S2(watch_set_sr_2_s2), .R2(watch_set_sr_2_r2), .S1(watch_set_sr_2_s1),
    .R1(watch_set_sr_2_r1), .S0(watch_set_sr_2_s0), .R0(watch_set_sr_2_r0), .SCO(watch_set_sr_2_sco),
    .RCO(watch_set_sr_2_rco));  // open: S3, R3
  count_rev_10 count_rev_10_2 (
    .Q3(HEURE[13]), .Q2(HEURE[12]), .Q1(HEURE[11]), .Q0(HEURE[10]), .U3(count_rev_10_2_u3),
    .U2(count_rev_10_2_u2), .U1(count_rev_10_2_u1), .U0(count_rev_10_2_u0), .CO(count_rev_10_2_co));
  WATCH_set_SR watch_set_sr_3 (
    .X0(SET_TIME[10]), .X1(SET_TIME[11]), .X2(SET_TIME[12]), .X3(SET_TIME[13]), .Y(SET_TIME[14]),
    .RESET(RESET), .EN(or_3_out), .S3(watch_set_sr_3_s3), .R3(watch_set_sr_3_r3), .S2(watch_set_sr_3_s2),
    .R2(watch_set_sr_3_r2), .S1(watch_set_sr_3_s1), .R1(watch_set_sr_3_r1), .S0(watch_set_sr_3_s0),
    .R0(watch_set_sr_3_r0), .SCO(watch_set_sr_3_sco), .RCO(watch_set_sr_3_rco));
  count_rev_6 count_rev_6_2 (
    .Q2(HEURE[17]), .Q1(HEURE[16]), .Q0(HEURE[15]), .U2(count_rev_6_2_u2), .U1(count_rev_6_2_u1),
    .U0(count_rev_6_2_u0), .CO(count_rev_6_2_co));
  WATCH_set_SR watch_set_sr_4 (
    .X0(SET_TIME[15]), .X1(SET_TIME[16]), .X2(SET_TIME[17]), .X3(SET_TIME[18]), .Y(SET_TIME[19]),
    .RESET(RESET), .EN(or_4_out), .S2(watch_set_sr_4_s2), .R2(watch_set_sr_4_r2), .S1(watch_set_sr_4_s1),
    .R1(watch_set_sr_4_r1), .S0(watch_set_sr_4_s0), .R0(watch_set_sr_4_r0), .SCO(watch_set_sr_4_sco),
    .RCO(watch_set_sr_4_rco));  // open: S3, R3
  count_rev_10_4 count_rev_10_4_1 (
    .H1(HEURE[26]), .H0(HEURE[25]), .Q3(HEURE[23]), .Q2(HEURE[22]), .Q1(HEURE[21]), .Q0(HEURE[20]),
    .U3(count_rev_10_4_1_u3), .U2(count_rev_10_4_1_u2), .U1(count_rev_10_4_1_u1), .U0(count_rev_10_4_1_u0),
    .CO(count_rev_10_4_1_co));
  WATCH_set_SR watch_set_sr_5 (
    .X0(SET_TIME[20]), .X1(SET_TIME[21]), .X2(SET_TIME[22]), .X3(SET_TIME[23]), .Y(SET_TIME[24]),
    .RESET(RESET), .EN(or_5_out), .S3(watch_set_sr_5_s3), .R3(watch_set_sr_5_r3), .S2(watch_set_sr_5_s2),
    .R2(watch_set_sr_5_r2), .S1(watch_set_sr_5_s1), .R1(watch_set_sr_5_r1), .S0(watch_set_sr_5_s0),
    .R0(watch_set_sr_5_r0), .SCO(watch_set_sr_5_sco), .RCO(watch_set_sr_5_rco));
  count_rev_3 count_rev_3_1 (.Q1(HEURE[26]), .Q0(HEURE[25]), .U1(count_rev_3_1_u1), .U0(count_rev_3_1_u0));  // open: CO
  WATCH_set_SR watch_set_sr_6 (
    .X0(SET_TIME[25]), .X1(SET_TIME[26]), .X2(SET_TIME[27]), .X3(SET_TIME[28]), .Y(SET_TIME[29]),
    .RESET(RESET), .EN(or_6_out), .S1(watch_set_sr_6_s1), .R1(watch_set_sr_6_r1), .S0(watch_set_sr_6_s0),
    .R0(watch_set_sr_6_r0));  // open: S3, R3, S2, R2, SCO, RCO
  D_Flip_Flop d_ff_1 (
    .D(count_rev_10_1_u3), .clk(multiplexer_2_out), .Q(HEURE[3]), .preset(watch_set_sr_1_s3),
    .reset(watch_set_sr_1_r3));  // open: Qn
  D_Flip_Flop d_ff_2 (
    .D(count_rev_10_1_u2), .clk(multiplexer_2_out), .Q(HEURE[2]), .preset(watch_set_sr_1_s2),
    .reset(watch_set_sr_1_r2));  // open: Qn
  D_Flip_Flop d_ff_3 (
    .D(count_rev_10_1_u1), .clk(multiplexer_2_out), .Q(HEURE[1]), .preset(watch_set_sr_1_s1),
    .reset(watch_set_sr_1_r1));  // open: Qn
  D_Flip_Flop d_ff_4 (
    .D(count_rev_10_1_u0), .clk(multiplexer_2_out), .Q(HEURE[0]), .preset(watch_set_sr_1_s0),
    .reset(watch_set_sr_1_r0));  // open: Qn
  D_Flip_Flop d_ff_5 (
    .D(count_rev_10_1_co), .clk(multiplexer_2_out), .Q(d_ff_5_q), .preset(watch_set_sr_1_sco),
    .reset(watch_set_sr_1_rco));  // open: Qn
  D_Flip_Flop d_ff_6 (
    .D(count_rev_6_1_u2), .clk(d_ff_5_q), .Q(HEURE[7]), .preset(watch_set_sr_2_s2), .reset(watch_set_sr_2_r2));  // open: Qn
  D_Flip_Flop d_ff_7 (
    .D(count_rev_6_1_u1), .clk(d_ff_5_q), .Q(HEURE[6]), .preset(watch_set_sr_2_s1), .reset(watch_set_sr_2_r1));  // open: Qn
  D_Flip_Flop d_ff_8 (
    .D(count_rev_6_1_u0), .clk(d_ff_5_q), .Q(HEURE[5]), .preset(watch_set_sr_2_s0), .reset(watch_set_sr_2_r0));  // open: Qn
  D_Flip_Flop d_ff_9 (
    .D(count_rev_6_1_co), .clk(d_ff_5_q), .Q(d_ff_9_q), .preset(watch_set_sr_2_sco),
    .reset(watch_set_sr_2_rco));  // open: Qn
  D_Flip_Flop d_ff_10 (
    .D(count_rev_10_2_u3), .clk(d_ff_9_q), .Q(HEURE[13]), .preset(watch_set_sr_3_s3),
    .reset(watch_set_sr_3_r3));  // open: Qn
  D_Flip_Flop d_ff_11 (
    .D(count_rev_10_2_u2), .clk(d_ff_9_q), .Q(HEURE[12]), .preset(watch_set_sr_3_s2),
    .reset(watch_set_sr_3_r2));  // open: Qn
  D_Flip_Flop d_ff_12 (
    .D(count_rev_10_2_u1), .clk(d_ff_9_q), .Q(HEURE[11]), .preset(watch_set_sr_3_s1),
    .reset(watch_set_sr_3_r1));  // open: Qn
  D_Flip_Flop d_ff_13 (
    .D(count_rev_10_2_u0), .clk(d_ff_9_q), .Q(HEURE[10]), .preset(watch_set_sr_3_s0),
    .reset(watch_set_sr_3_r0));  // open: Qn
  D_Flip_Flop d_ff_14 (
    .D(count_rev_10_2_co), .clk(d_ff_9_q), .Q(d_ff_14_q), .preset(watch_set_sr_3_sco),
    .reset(watch_set_sr_3_rco));  // open: Qn
  D_Flip_Flop d_ff_15 (
    .D(count_rev_6_2_u2), .clk(d_ff_14_q), .Q(HEURE[17]), .preset(watch_set_sr_4_s2),
    .reset(watch_set_sr_4_r2));  // open: Qn
  D_Flip_Flop d_ff_16 (
    .D(count_rev_6_2_u1), .clk(d_ff_14_q), .Q(HEURE[16]), .preset(watch_set_sr_4_s1),
    .reset(watch_set_sr_4_r1));  // open: Qn
  D_Flip_Flop d_ff_17 (
    .D(count_rev_6_2_u0), .clk(d_ff_14_q), .Q(HEURE[15]), .preset(watch_set_sr_4_s0),
    .reset(watch_set_sr_4_r0));  // open: Qn
  D_Flip_Flop d_ff_18 (
    .D(count_rev_6_2_co), .clk(d_ff_14_q), .Q(d_ff_18_q), .preset(watch_set_sr_4_sco),
    .reset(watch_set_sr_4_rco));  // open: Qn
  D_Flip_Flop d_ff_19 (
    .D(count_rev_10_4_1_u3), .clk(d_ff_18_q), .Q(HEURE[23]), .preset(watch_set_sr_5_s3),
    .reset(watch_set_sr_5_r3));  // open: Qn
  D_Flip_Flop d_ff_20 (
    .D(count_rev_10_4_1_u2), .clk(d_ff_18_q), .Q(HEURE[22]), .preset(watch_set_sr_5_s2),
    .reset(watch_set_sr_5_r2));  // open: Qn
  D_Flip_Flop d_ff_21 (
    .D(count_rev_10_4_1_u1), .clk(d_ff_18_q), .Q(HEURE[21]), .preset(watch_set_sr_5_s1),
    .reset(watch_set_sr_5_r1));  // open: Qn
  D_Flip_Flop d_ff_22 (
    .D(count_rev_10_4_1_u0), .clk(d_ff_18_q), .Q(HEURE[20]), .preset(watch_set_sr_5_s0),
    .reset(watch_set_sr_5_r0));  // open: Qn
  D_Flip_Flop d_ff_23 (
    .D(count_rev_10_4_1_co), .clk(d_ff_18_q), .Q(d_ff_23_q), .preset(watch_set_sr_5_sco),
    .reset(watch_set_sr_5_rco));  // open: Qn
  D_Flip_Flop d_ff_24 (
    .D(count_rev_3_1_u1), .clk(d_ff_23_q), .Q(HEURE[26]), .preset(watch_set_sr_6_s1),
    .reset(watch_set_sr_6_r1));  // open: Qn
  D_Flip_Flop d_ff_25 (
    .D(count_rev_3_1_u0), .clk(d_ff_23_q), .Q(HEURE[25]), .preset(watch_set_sr_6_s0),
    .reset(watch_set_sr_6_r0));  // open: Qn
  ALARM_compare alarm_compare_1 (
    .HEURE({3'b000, HEURE[26:25], 1'b1, HEURE[23:20], 2'b00, HEURE[17:15], 1'b1, HEURE[13:10], 2'b00, HEURE[7:5], 1'b1, HEURE[3:0]}),
    .SET_TIME(30'h1004010), .EN_BUZZER(alarm_compare_1_en_buzzer));
  not not_3 (not_3_out, alarm_compare_1_en_buzzer);
  and and_4 (and_4_out, chrono_start_stop_1_q, not_3_out);
  S_R_Flip_Flop s_r_ff_1 (.Q(s_r_ff_1_q), .reset(or_7_out), .preset(and_4_out));  // open: S, R, clk, Qn
  or or_7 (or_7_out, RESET, StartStop);
  Multiplexer #(.enable("false")) multiplexer_3 (
    .in0(1'b0), .in1(alarm_compare_1_en_buzzer), .out(EN_buzzer), .sel(s_r_ff_1_q));

  assign {HEURE[29:27], HEURE[24], HEURE[19:18], HEURE[14], HEURE[9:8], HEURE[4]} = 10'h49;

  // Notes on the sheet:
  //   secondes (unités)
  //   secondes (dizaines)
  //   minutes (unités)
  //   minutes (dizaines)
  //   heures (unités)
  //   heures (dizaines)
endmodule

module TIMESET (
  input  [4:0] NUMBER,
  input  data_ready,
  input  reset,
  input  B2,
  input  display,
  output [29:0] SET_TIME,
  output EN_set
);

  and and_1 (EN_set, B2, display);
  shift_register shift_register_1 (
    .N0(NUMBER[0]), .N1(NUMBER[1]), .N2(NUMBER[2]), .N3(NUMBER[3]), .clock(data_ready), .R(reset),
    .SET_TIME(SET_TIME));
endmodule

module TIMESET_display (
  input  RESET,
  input  display,
  input  B1,
  input  B2,
  input  B2_long,
  output x
);

  wire timeset_sr_1_r, timeset_sr_1_s;

  TIMESET_SR timeset_sr_1 (
    .RESET(RESET), .display(display), .B1(B1), .B2(B2), .B2_long(B2_long), .S(timeset_sr_1_s),
    .R(timeset_sr_1_r));
  S_R_Flip_Flop s_r_ff_1 (.Q(x), .reset(timeset_sr_1_r), .preset(timeset_sr_1_s));  // open: S, R, clk, Qn
endmodule

module TIMESET_SR (
  input  RESET,
  input  display,
  input  B1,
  input  B2,
  input  B2_long,
  output S,
  output R
);

  wire and_1_out, and_2_out, and_3_out, and_4_out, and_5_out, and_6_out, not_1_out, not_2_out, not_3_out,
       not_4_out, not_5_out;

  not not_1 (not_1_out, RESET);
  not not_2 (not_2_out, display);
  not not_3 (not_3_out, B1);
  not not_4 (not_4_out, B2);
  not not_5 (not_5_out, B2_long);
  and and_1 (and_1_out, not_1_out, not_2_out, B2_long);
  and and_2 (and_2_out, not_1_out, display, not_3_out, not_4_out);
  and and_3 (and_3_out, not_1_out, display, B1, B2);
  and and_4 (and_4_out, not_2_out, not_5_out);
  and and_5 (and_5_out, display, not_3_out, B2);
  and and_6 (and_6_out, display, B1, not_4_out);
  or or_1 (S, and_1_out, and_2_out, and_3_out);
  or or_2 (R, and_4_out, and_5_out, and_6_out, RESET);
endmodule

module The_Imperial_March (
  input  ONOFF,
  input  EN_buzzer,
  input  RESET,
  output V,
  output GND
);

  wire and_1_out, BPM_out, clock_1_out, clock_2_out, clock_3_out, clock_4_out, clock_5_out, clock_6_out,
       d_ff_1_q, d_ff_2_q, d_ff_3_q, d_ff_4_q, d_ff_5_q, d_ff_6_q, d_ff_7_q, d_ff_8_q, d_ff_9_q, d_ff_10_q,
       d_ff_11_q, d_ff_12_q, d_ff_13_q, d_ff_14_q, d_ff_15_q, d_ff_16_q, d_ff_17_q, d_ff_18_q, d_ff_19_q,
       d_ff_20_q, d_ff_21_q, d_ff_22_q, d_ff_23_q, d_ff_24_q, d_ff_25_q, d_ff_26_q, d_ff_27_q, d_ff_28_q,
       d_ff_29_q, d_ff_30_q, d_ff_31_q, d_ff_32_q, d_ff_33_q, d_ff_34_q, d_ff_35_q, d_ff_36_q, d_ff_37_q,
       d_ff_38_q, d_ff_39_q, d_ff_40_q, d_ff_41_q, d_ff_42_q, d_ff_43_q, d_ff_44_q, d_ff_45_q, d_ff_46_q,
       d_ff_47_q, d_ff_48_q, d_ff_49_q, d_ff_50_q, d_ff_51_q, d_ff_52_q, d_ff_53_q, d_ff_54_q, d_ff_55_q,
       d_ff_56_q, d_ff_57_q, d_ff_58_q, d_ff_59_q, d_ff_60_q, d_ff_61_q, d_ff_62_q, d_ff_63_q, d_ff_64_q,
       multiplexer_1_out, multiplexer_2_out, multiplexer_3_out, multiplexer_4_out, multiplexer_5_out,
       multiplexer_6_out, multiplexer_7_out, or_1_out, or_2_out, or_3_out, or_4_out, or_5_out, or_6_out;

  Clock #(.highDuration(1600), .lowDuration(1600)) BPM (.out(BPM_out));
  Multiplexer #(.enable("false")) multiplexer_1 (.in0(1'b0), .in1(BPM_out), .out(multiplexer_1_out), .sel(and_1_out));
  and and_1 (and_1_out, ONOFF, EN_buzzer);
  D_Flip_Flop d_ff_1 (.D(d_ff_64_q), .clk(multiplexer_1_out), .Q(d_ff_1_q), .reset(RESET));  // open: Qn, preset
  D_Flip_Flop d_ff_2 (.D(d_ff_49_q), .clk(multiplexer_1_out), .Q(d_ff_2_q), .reset(RESET));  // open: Qn, preset
  D_Flip_Flop d_ff_3 (.D(d_ff_50_q), .clk(multiplexer_1_out), .Q(d_ff_3_q), .reset(RESET));  // open: Qn, preset
  D_Flip_Flop d_ff_4 (.D(d_ff_51_q), .clk(multiplexer_1_out), .Q(d_ff_4_q), .reset(RESET));  // open: Qn, preset
  D_Flip_Flop d_ff_5 (.D(d_ff_52_q), .clk(multiplexer_1_out), .Q(d_ff_5_q), .reset(RESET));  // open: Qn, preset
  D_Flip_Flop d_ff_6 (.D(d_ff_53_q), .clk(multiplexer_1_out), .Q(d_ff_6_q), .reset(RESET));  // open: Qn, preset
  D_Flip_Flop d_ff_7 (.D(d_ff_54_q), .clk(multiplexer_1_out), .Q(d_ff_7_q), .reset(RESET));  // open: Qn, preset
  D_Flip_Flop d_ff_8 (.D(d_ff_55_q), .clk(multiplexer_1_out), .Q(d_ff_8_q), .reset(RESET));  // open: Qn, preset
  D_Flip_Flop d_ff_9 (.D(d_ff_56_q), .clk(multiplexer_1_out), .Q(d_ff_9_q), .reset(RESET));  // open: Qn, preset
  D_Flip_Flop d_ff_10 (.D(d_ff_57_q), .clk(multiplexer_1_out), .Q(d_ff_10_q), .reset(RESET));  // open: Qn, preset
  D_Flip_Flop d_ff_11 (.D(d_ff_58_q), .clk(multiplexer_1_out), .Q(d_ff_11_q), .reset(RESET));  // open: Qn, preset
  D_Flip_Flop d_ff_12 (.D(d_ff_59_q), .clk(multiplexer_1_out), .Q(d_ff_12_q), .reset(RESET));  // open: Qn, preset
  D_Flip_Flop d_ff_13 (.D(d_ff_60_q), .clk(multiplexer_1_out), .Q(d_ff_13_q), .reset(RESET));  // open: Qn, preset
  D_Flip_Flop d_ff_14 (.D(d_ff_61_q), .clk(multiplexer_1_out), .Q(d_ff_14_q), .reset(RESET));  // open: Qn, preset
  D_Flip_Flop d_ff_15 (.D(d_ff_62_q), .clk(multiplexer_1_out), .Q(d_ff_15_q), .reset(RESET));  // open: Qn, preset
  D_Flip_Flop d_ff_16 (.D(d_ff_63_q), .clk(multiplexer_1_out), .Q(d_ff_16_q), .reset(RESET));  // open: Qn, preset
  D_Flip_Flop d_ff_17 (.D(d_ff_1_q), .clk(multiplexer_1_out), .Q(d_ff_17_q), .reset(RESET));  // open: Qn, preset
  D_Flip_Flop d_ff_18 (.D(d_ff_2_q), .clk(multiplexer_1_out), .Q(d_ff_18_q), .reset(RESET));  // open: Qn, preset
  D_Flip_Flop d_ff_19 (.D(d_ff_3_q), .clk(multiplexer_1_out), .Q(d_ff_19_q), .reset(RESET));  // open: Qn, preset
  D_Flip_Flop d_ff_20 (.D(d_ff_4_q), .clk(multiplexer_1_out), .Q(d_ff_20_q), .reset(RESET));  // open: Qn, preset
  D_Flip_Flop d_ff_21 (.D(d_ff_5_q), .clk(multiplexer_1_out), .Q(d_ff_21_q), .reset(RESET));  // open: Qn, preset
  D_Flip_Flop d_ff_22 (.D(d_ff_6_q), .clk(multiplexer_1_out), .Q(d_ff_22_q), .reset(RESET));  // open: Qn, preset
  D_Flip_Flop d_ff_23 (.D(d_ff_7_q), .clk(multiplexer_1_out), .Q(d_ff_23_q), .reset(RESET));  // open: Qn, preset
  D_Flip_Flop d_ff_24 (.D(d_ff_8_q), .clk(multiplexer_1_out), .Q(d_ff_24_q), .reset(RESET));  // open: Qn, preset
  D_Flip_Flop d_ff_25 (.D(d_ff_9_q), .clk(multiplexer_1_out), .Q(d_ff_25_q), .reset(RESET));  // open: Qn, preset
  D_Flip_Flop d_ff_26 (.D(d_ff_10_q), .clk(multiplexer_1_out), .Q(d_ff_26_q), .reset(RESET));  // open: Qn, preset
  D_Flip_Flop d_ff_27 (.D(d_ff_11_q), .clk(multiplexer_1_out), .Q(d_ff_27_q), .reset(RESET));  // open: Qn, preset
  D_Flip_Flop d_ff_28 (.D(d_ff_12_q), .clk(multiplexer_1_out), .Q(d_ff_28_q), .reset(RESET));  // open: Qn, preset
  D_Flip_Flop d_ff_29 (.D(d_ff_13_q), .clk(multiplexer_1_out), .Q(d_ff_29_q), .reset(RESET));  // open: Qn, preset
  D_Flip_Flop d_ff_30 (.D(d_ff_14_q), .clk(multiplexer_1_out), .Q(d_ff_30_q), .reset(RESET));  // open: Qn, preset
  D_Flip_Flop d_ff_31 (.D(d_ff_15_q), .clk(multiplexer_1_out), .Q(d_ff_31_q), .reset(RESET));  // open: Qn, preset
  D_Flip_Flop d_ff_32 (.D(d_ff_16_q), .clk(multiplexer_1_out), .Q(d_ff_32_q), .reset(RESET));  // open: Qn, preset
  D_Flip_Flop d_ff_33 (.D(d_ff_17_q), .clk(multiplexer_1_out), .Q(d_ff_33_q), .reset(RESET));  // open: Qn, preset
  D_Flip_Flop d_ff_34 (.D(d_ff_18_q), .clk(multiplexer_1_out), .Q(d_ff_34_q), .reset(RESET));  // open: Qn, preset
  D_Flip_Flop d_ff_35 (.D(d_ff_19_q), .clk(multiplexer_1_out), .Q(d_ff_35_q), .reset(RESET));  // open: Qn, preset
  D_Flip_Flop d_ff_36 (.D(d_ff_20_q), .clk(multiplexer_1_out), .Q(d_ff_36_q), .reset(RESET));  // open: Qn, preset
  D_Flip_Flop d_ff_37 (.D(d_ff_21_q), .clk(multiplexer_1_out), .Q(d_ff_37_q), .reset(RESET));  // open: Qn, preset
  D_Flip_Flop d_ff_38 (.D(d_ff_22_q), .clk(multiplexer_1_out), .Q(d_ff_38_q), .reset(RESET));  // open: Qn, preset
  D_Flip_Flop d_ff_39 (.D(d_ff_23_q), .clk(multiplexer_1_out), .Q(d_ff_39_q), .reset(RESET));  // open: Qn, preset
  D_Flip_Flop d_ff_40 (.D(d_ff_24_q), .clk(multiplexer_1_out), .Q(d_ff_40_q), .reset(RESET));  // open: Qn, preset
  D_Flip_Flop d_ff_41 (.D(d_ff_25_q), .clk(multiplexer_1_out), .Q(d_ff_41_q), .reset(RESET));  // open: Qn, preset
  D_Flip_Flop d_ff_42 (.D(d_ff_26_q), .clk(multiplexer_1_out), .Q(d_ff_42_q), .reset(RESET));  // open: Qn, preset
  D_Flip_Flop d_ff_43 (.D(d_ff_27_q), .clk(multiplexer_1_out), .Q(d_ff_43_q), .reset(RESET));  // open: Qn, preset
  D_Flip_Flop d_ff_44 (.D(d_ff_28_q), .clk(multiplexer_1_out), .Q(d_ff_44_q), .reset(RESET));  // open: Qn, preset
  D_Flip_Flop d_ff_45 (.D(d_ff_29_q), .clk(multiplexer_1_out), .Q(d_ff_45_q), .reset(RESET));  // open: Qn, preset
  D_Flip_Flop d_ff_46 (.D(d_ff_30_q), .clk(multiplexer_1_out), .Q(d_ff_46_q), .reset(RESET));  // open: Qn, preset
  D_Flip_Flop d_ff_47 (.D(d_ff_31_q), .clk(multiplexer_1_out), .Q(d_ff_47_q), .reset(RESET));  // open: Qn, preset
  D_Flip_Flop d_ff_48 (.D(d_ff_32_q), .clk(multiplexer_1_out), .Q(d_ff_48_q), .reset(RESET));  // open: Qn, preset
  D_Flip_Flop d_ff_49 (.D(d_ff_33_q), .clk(multiplexer_1_out), .Q(d_ff_49_q), .reset(RESET));  // open: Qn, preset
  D_Flip_Flop d_ff_50 (.D(d_ff_34_q), .clk(multiplexer_1_out), .Q(d_ff_50_q), .reset(RESET));  // open: Qn, preset
  D_Flip_Flop d_ff_51 (.D(d_ff_35_q), .clk(multiplexer_1_out), .Q(d_ff_51_q), .reset(RESET));  // open: Qn, preset
  D_Flip_Flop d_ff_52 (.D(d_ff_36_q), .clk(multiplexer_1_out), .Q(d_ff_52_q), .reset(RESET));  // open: Qn, preset
  D_Flip_Flop d_ff_53 (.D(d_ff_37_q), .clk(multiplexer_1_out), .Q(d_ff_53_q), .reset(RESET));  // open: Qn, preset
  D_Flip_Flop d_ff_54 (.D(d_ff_38_q), .clk(multiplexer_1_out), .Q(d_ff_54_q), .reset(RESET));  // open: Qn, preset
  D_Flip_Flop d_ff_55 (.D(d_ff_39_q), .clk(multiplexer_1_out), .Q(d_ff_55_q), .reset(RESET));  // open: Qn, preset
  D_Flip_Flop d_ff_56 (.D(d_ff_40_q), .clk(multiplexer_1_out), .Q(d_ff_56_q), .reset(RESET));  // open: Qn, preset
  D_Flip_Flop d_ff_57 (.D(d_ff_41_q), .clk(multiplexer_1_out), .Q(d_ff_57_q), .reset(RESET));  // open: Qn, preset
  D_Flip_Flop d_ff_58 (.D(d_ff_42_q), .clk(multiplexer_1_out), .Q(d_ff_58_q), .reset(RESET));  // open: Qn, preset
  D_Flip_Flop d_ff_59 (.D(d_ff_43_q), .clk(multiplexer_1_out), .Q(d_ff_59_q), .reset(RESET));  // open: Qn, preset
  D_Flip_Flop d_ff_60 (.D(d_ff_44_q), .clk(multiplexer_1_out), .Q(d_ff_60_q), .reset(RESET));  // open: Qn, preset
  D_Flip_Flop d_ff_61 (.D(d_ff_45_q), .clk(multiplexer_1_out), .Q(d_ff_61_q), .reset(RESET));  // open: Qn, preset
  D_Flip_Flop d_ff_62 (.D(d_ff_46_q), .clk(multiplexer_1_out), .Q(d_ff_62_q), .reset(RESET));  // open: Qn, preset
  D_Flip_Flop d_ff_63 (.D(d_ff_47_q), .clk(multiplexer_1_out), .Q(d_ff_63_q), .reset(RESET));  // open: Qn, preset
  D_Flip_Flop d_ff_64 (.D(d_ff_48_q), .clk(multiplexer_1_out), .Q(d_ff_64_q), .preset(RESET));  // open: Qn, reset
  Clock #(.highDuration(31), .lowDuration(31)) clock_1 (.out(clock_1_out));
  or or_1 (or_1_out, d_ff_52_q, d_ff_54_q, d_ff_60_q, d_ff_62_q);
  Clock #(.highDuration(36), .lowDuration(36)) clock_2 (.out(clock_2_out));
  or or_2 (or_2_out, d_ff_1_q, d_ff_17_q, d_ff_2_q, d_ff_18_q, d_ff_3_q, d_ff_19_q, d_ff_5_q, d_ff_21_q, d_ff_7_q, d_ff_23_q, d_ff_39_q, d_ff_55_q, d_ff_15_q, d_ff_31_q, d_ff_47_q, d_ff_63_q);
  Multiplexer #(.enable("false")) multiplexer_2 (
    .in0(1'b0), .in1(clock_1_out), .out(multiplexer_2_out), .sel(or_1_out));
  Multiplexer #(.enable("false")) multiplexer_3 (
    .in0(1'b0), .in1(clock_2_out), .out(multiplexer_3_out), .sel(or_2_out));
  Multiplexer #(.enable("false")) multiplexer_4 (
    .in0(1'b0), .in1(clock_3_out), .out(multiplexer_4_out), .sel(or_3_out));
  Clock #(.highDuration(46), .lowDuration(46)) clock_3 (.out(clock_3_out));
  or or_3 (or_3_out, d_ff_4_q, d_ff_20_q, d_ff_6_q, d_ff_22_q, d_ff_14_q, d_ff_30_q);
  Clock #(.highDuration(24), .lowDuration(24)) clock_4 (.out(clock_4_out));
  or or_4 (or_4_out, d_ff_9_q, d_ff_25_q, d_ff_10_q, d_ff_26_q, d_ff_11_q, d_ff_27_q);
  Multiplexer #(.enable("false")) multiplexer_5 (
    .in0(1'b0), .in1(clock_5_out), .out(multiplexer_5_out), .sel(or_5_out));
  Clock #(.highDuration(18), .lowDuration(18)) clock_5 (.out(clock_5_out));
  or or_5 (or_5_out, d_ff_12_q, d_ff_28_q);
  Multiplexer #(.enable("false")) multiplexer_6 (
    .in0(1'b0), .in1(clock_6_out), .out(multiplexer_6_out), .sel(or_6_out));
  Clock #(.highDuration(39), .lowDuration(39)) clock_6 (.out(clock_6_out));
  or or_6 (or_6_out, d_ff_13_q, d_ff_29_q);
  Multiplexer #(.enable("false")) multiplexer_7 (
    .in0(1'b0), .in1(clock_4_out), .out(multiplexer_7_out), .sel(or_4_out));
  or or_7 (V, multiplexer_2_out, multiplexer_3_out, multiplexer_4_out, multiplexer_7_out, multiplexer_5_out, multiplexer_6_out);

  assign GND = 1'b0;

  // Notes on the sheet:
  //   DO
  //   LA
  //   FA
  //   MI
  //   FA'
  //   LAb
endmodule

module BUZZ (
  input  ONOFF,
  input  EN_BUZZER,
  output V,
  output GND
);

  wire clock_1_out, not_1_out, t_ff_1_q;

  not not_1 (not_1_out, ONOFF);
  Clock #(.highDuration(23), .lowDuration(23)) clock_1 (.out(clock_1_out));
  T_Flip_Flop t_ff_1 (.Q(t_ff_1_q), .reset(not_1_out), .preset(EN_BUZZER));  // open: T, clk, Qn
  Multiplexer #(.enable("false")) multiplexer_1 (.in0(1'b0), .in1(clock_1_out), .out(V), .sel(t_ff_1_q));

  assign GND = 1'b0;
endmodule

module KEYPAD (
  input  RESET,
  input  y1,
  input  y2,
  input  y3,
  input  y4,
  output x1,
  output x2,
  output x3,
  output x4,
  output [4:0] NUMBER,
  output data_ready
);

  wire keypad_debounce_4_1_ch0_dout, keypad_debounce_4_1_ch1_dout, keypad_debounce_4_1_ch2_dout,
       keypad_debounce_4_1_ch3_dout, keypad_fsm_full_1_output_1, keypad_fsm_full_1_output_2,
       keypad_fsm_full_1_output_3, keypad_fsm_full_1_output_4, keypad_register_8bit_1_output_1,
       keypad_register_8bit_1_output_2, keypad_register_8bit_1_output_3, keypad_register_8bit_1_output_4,
       keypad_register_8bit_1_output_5, keypad_register_8bit_1_output_6, keypad_register_8bit_1_output_7,
       keypad_register_8bit_1_output_8, keypad_state_0_1_hp_s0_detect, keypad_state_1_1_hp_s0_detect,
       keypad_state_2_1_hp_s2_data_ready, keypad_state_3_1_timer_out, not_1_out, not_2_out, not_3_out,
       not_4_out, not_5_out, not_6_out, not_7_out, not_8_out, or_1_out;

  Clock sysclk ();  // open: out
  Clock #(.highDuration(10), .lowDuration(10)) clk_256 ();  // open: out
  Clock #(.highDuration(100), .lowDuration(100)) clk_16 ();  // open: out
  KEYPAD_fsm_full keypad_fsm_full_1 (
    .i01_Hpulse(keypad_state_0_1_hp_s0_detect), .i02_Hpulse(keypad_state_1_1_hp_s0_detect),
    .i03_Hpulse(keypad_state_2_1_hp_s2_data_ready), .Input_1(keypad_state_3_1_timer_out), .RESET(RESET),
    .Output_1(keypad_fsm_full_1_output_1), .Output_2(keypad_fsm_full_1_output_2),
    .Output_3(keypad_fsm_full_1_output_3), .Output_4(keypad_fsm_full_1_output_4));
  KEYPAD_debounce_4 keypad_debounce_4_1 (
    .ch0(y1), .ch1(y2), .ch2(y3), .ch3(y4), .RESET(RESET), .ch0_dout(keypad_debounce_4_1_ch0_dout),
    .ch1_dout(keypad_debounce_4_1_ch1_dout), .ch2_dout(keypad_debounce_4_1_ch2_dout),
    .ch3_dout(keypad_debounce_4_1_ch3_dout));
  KEYPAD_state_0 keypad_state_0_1 (
    .S0(keypad_fsm_full_1_output_1), .RESET(RESET), .y1(keypad_debounce_4_1_ch0_dout),
    .y2(keypad_debounce_4_1_ch1_dout), .y3(keypad_debounce_4_1_ch2_dout), .y4(keypad_debounce_4_1_ch3_dout),
    .HP_S0_detect(keypad_state_0_1_hp_s0_detect));
  KEYPAD_state_1 keypad_state_1_1 (
    .s1(keypad_fsm_full_1_output_2), .RESET(RESET), .y1(keypad_debounce_4_1_ch0_dout),
    .y2(keypad_debounce_4_1_ch1_dout), .y3(keypad_debounce_4_1_ch2_dout), .y4(keypad_debounce_4_1_ch3_dout),
    .HP_S0_detect(keypad_state_1_1_hp_s0_detect), .coldriver0(x1), .coldriver1(x2), .coldriver2(x3),
    .coldriver3(x4));
  KEYPAD_register_8bit keypad_register_8bit_1 (
    .clk01(keypad_state_0_1_hp_s0_detect), .clk02(keypad_state_1_1_hp_s0_detect), .RESET(RESET),
    .b0(keypad_debounce_4_1_ch0_dout), .b1(keypad_debounce_4_1_ch1_dout), .b2(keypad_debounce_4_1_ch2_dout),
    .b3(keypad_debounce_4_1_ch3_dout), .b4(x1), .b5(x2), .b6(x3), .b7(x4),
    .Output_1(keypad_register_8bit_1_output_1), .Output_2(keypad_register_8bit_1_output_2),
    .Output_3(keypad_register_8bit_1_output_3), .Output_4(keypad_register_8bit_1_output_4),
    .Output_5(keypad_register_8bit_1_output_5), .Output_6(keypad_register_8bit_1_output_6),
    .Output_7(keypad_register_8bit_1_output_7), .Output_8(keypad_register_8bit_1_output_8));
  KEYPAD_state_2 keypad_state_2_1 (
    .s2(keypad_fsm_full_1_output_3), .RESET(RESET), .HP_S2_data_ready(keypad_state_2_1_hp_s2_data_ready));
  KEYPAD_state_3 keypad_state_3_1 (
    .s3(keypad_fsm_full_1_output_4), .RESET(RESET), .timer_out(keypad_state_3_1_timer_out));
  not not_1 (not_1_out, keypad_register_8bit_1_output_1);
  not not_2 (not_2_out, keypad_register_8bit_1_output_2);
  not not_3 (not_3_out, keypad_register_8bit_1_output_3);
  not not_4 (not_4_out, keypad_register_8bit_1_output_4);
  not not_5 (not_5_out, keypad_register_8bit_1_output_5);
  not not_6 (not_6_out, keypad_register_8bit_1_output_6);
  not not_7 (not_7_out, keypad_register_8bit_1_output_7);
  not not_8 (not_8_out, keypad_register_8bit_1_output_8);
  or or_1 (or_1_out, keypad_state_3_1_timer_out, RESET);
  D_Flip_Flop d_ff_1 (
    .D(1'b0), .clk(1'b0), .Q(data_ready), .preset(keypad_state_2_1_hp_s2_data_ready), .reset(or_1_out));  // open: Qn
  KEYPAD_decodeur keypad_decodeur_1 (
    .Y1(not_1_out), .Y2(not_2_out), .Y3(not_3_out), .Y4(not_4_out), .Input_1(not_5_out), .Input_2(not_6_out),
    .Input_3(not_7_out), .X4(not_8_out), .x0(NUMBER[0]), .x1(NUMBER[1]), .x2(NUMBER[2]), .x3(NUMBER[3]));

  assign NUMBER[4] = 1'b0;

  // Notes on the sheet:
  //   1 = doite, 8 = gauche
  //   1 = Y1
  //   2 = Y2
  //   3 = Y3
  //   4 = Y4
  //   5 = X1
  //   6 = X2
  //   7 = X3
  //   8 = X4
endmodule

module KEYPAD_fsm_full (
  input  i01_Hpulse,
  input  i02_Hpulse,
  input  i03_Hpulse,
  input  Input_1,
  input  RESET,
  output Output_1,
  output Output_2,
  output Output_3,
  output Output_4
);

  wire or_1_out;

  Clock sysclk ();  // open: out
  or or_1 (or_1_out, i01_Hpulse, i02_Hpulse, i03_Hpulse, Input_1);
  D_Flip_Flop d_ff_1 (.D(Output_4), .clk(or_1_out), .Q(Output_1), .preset(RESET));  // open: Qn, reset
  D_Flip_Flop d_ff_2 (.D(Output_1), .clk(or_1_out), .Q(Output_2), .reset(RESET));  // open: Qn, preset
  D_Flip_Flop d_ff_3 (.D(Output_2), .clk(or_1_out), .Q(Output_3), .reset(RESET));  // open: Qn, preset
  D_Flip_Flop d_ff_4 (.D(Output_3), .clk(or_1_out), .Q(Output_4), .reset(RESET));  // open: Qn, preset

  // Notes on the sheet:
  //   Transition logic
  //   (active on a positive pulse)
  //   A Moore finite-state machine and its decoder are optimized into a simplified circuit presented here
  //   Counter and decoder
  //   (optimized/simplified into one circuit)
endmodule

module KEYPAD_state_0 (
  input  S0,
  input  RESET,
  input  y1,
  input  y2,
  input  y3,
  input  y4,
  output HP_S0_detect
);

  wire and_1_out, and_2_out, clk_256_out, d_ff_1_q, d_ff_2_q, d_ff_3_q, not_1_out, or_1_out, xor_1_out;

  Clock sysclk ();  // open: out
  Clock #(.highDuration(10), .lowDuration(10)) clk_256 (.out(clk_256_out));
  not not_1 (not_1_out, S0);
  or or_1 (or_1_out, not_1_out, RESET);
  and and_1 (and_1_out, y1, y2, y3, y4);
  D_Flip_Flop d_ff_1 (.D(and_1_out), .clk(clk_256_out), .Q(d_ff_1_q), .reset(or_1_out));  // open: Qn, preset
  xor xor_1 (xor_1_out, and_1_out, d_ff_1_q);
  D_Flip_Flop d_ff_2 (.D(and_2_out), .clk(clk_256_out), .Q(d_ff_2_q), .reset(or_1_out));  // open: Qn, preset
  and and_2 (and_2_out, xor_1_out, d_ff_1_q);
  D_Flip_Flop d_ff_3 (.D(d_ff_2_q), .clk(clk_256_out), .Q(d_ff_3_q), .reset(or_1_out));  // open: Qn, preset
  xor xor_2 (HP_S0_detect, d_ff_2_q, d_ff_3_q);
endmodule

module KEYPAD_state_1 (
  input  s1,
  input  RESET,
  input  y1,
  input  y2,
  input  y3,
  input  y4,
  output HP_S0_detect,
  output coldriver0,
  output coldriver1,
  output coldriver2,
  output coldriver3
);

  wire and_1_out, and_2_out, and_3_out, and_4_out, clk_16_out, clk_256_out, d_ff_1_qn, d_ff_2_q, d_ff_2_qn,
       d_ff_3_q, d_ff_4_q, d_ff_5_q, d_ff_6_q, d_ff_7_q, d_ff_8_q, d_ff_9_q, d_ff_9_qn, not_1_out, or_1_out,
       or_2_out, xor_1_out, xor_2_out, xor_4_out;

  Clock sysclk ();  // open: out
  Clock #(.highDuration(10), .lowDuration(10)) clk_256 (.out(clk_256_out));
  Clock #(.highDuration(100), .lowDuration(100)) clk_16 (.out(clk_16_out));
  not not_1 (not_1_out, s1);
  or or_1 (or_1_out, not_1_out, RESET);
  and and_1 (and_1_out, y1, y2, y3, y4);
  and and_2 (and_2_out, d_ff_9_q, clk_16_out);
  D_Flip_Flop d_ff_1 (.D(s1), .clk(clk_256_out), .Qn(d_ff_1_qn), .reset(or_1_out));  // open: Q, preset
  D_Flip_Flop d_ff_2 (
    .D(and_1_out), .clk(clk_256_out), .Q(d_ff_2_q), .Qn(d_ff_2_qn), .reset(or_2_out));  // open: preset
  or or_2 (or_2_out, or_1_out, d_ff_9_qn);
  D_Flip_Flop d_ff_3 (.D(and_3_out), .clk(clk_256_out), .Q(d_ff_3_q), .reset(or_1_out));  // open: Qn, preset
  and and_3 (and_3_out, s1, d_ff_1_qn);
  xor xor_1 (xor_1_out, and_1_out, d_ff_2_q);
  D_Flip_Flop d_ff_4 (.D(and_4_out), .clk(clk_256_out), .Q(d_ff_4_q), .reset(or_2_out));  // open: Qn, preset
  and and_4 (and_4_out, xor_1_out, d_ff_2_q);
  D_Flip_Flop d_ff_5 (.D(d_ff_3_q), .clk(clk_256_out), .Q(d_ff_5_q), .reset(or_1_out));  // open: Qn, preset
  D_Flip_Flop d_ff_6 (.D(d_ff_4_q), .clk(clk_256_out), .Q(d_ff_6_q), .reset(or_2_out));  // open: Qn, preset
  xor xor_2 (xor_2_out, d_ff_3_q, d_ff_5_q);
  D_Flip_Flop d_ff_7 (.D(d_ff_5_q), .clk(clk_256_out), .Q(d_ff_7_q), .reset(or_1_out));  // open: Qn, preset
  D_Flip_Flop d_ff_8 (.D(d_ff_7_q), .clk(clk_256_out), .Q(d_ff_8_q), .reset(or_1_out));  // open: Qn, preset
  xor xor_3 (HP_S0_detect, d_ff_4_q, d_ff_6_q);
  xor xor_4 (xor_4_out, d_ff_7_q, d_ff_8_q);
  D_Flip_Flop d_ff_9 (.Q(d_ff_9_q), .Qn(d_ff_9_qn), .preset(xor_4_out), .reset(or_1_out));  // open: D, clk
  KEYPAD_bubble_counter keypad_bubble_counter_1 (
    .R(or_1_out), .S(xor_2_out), .clk(and_2_out), .colddriver0(coldriver0), .colddriver1(coldriver1),
    .colddriver2(coldriver2), .colddriver3(coldriver3));
endmodule

module KEYPAD_state_2 (
  input  s2,
  input  RESET,
  output HP_S2_data_ready
);

  wire clk_256_out, d_ff_1_q, d_ff_2_q, d_ff_3_q, not_1_out, or_1_out;

  Clock sysclk ();  // open: out
  Clock #(.highDuration(10), .lowDuration(10)) clk_256 (.out(clk_256_out));
  not not_1 (not_1_out, s2);
  or or_1 (or_1_out, not_1_out, RESET);
  D_Flip_Flop d_ff_1 (.D(1'b0), .clk(clk_256_out), .Q(d_ff_1_q), .preset(or_1_out));  // open: Qn, reset
  D_Flip_Flop d_ff_2 (.D(d_ff_1_q), .clk(clk_256_out), .Q(d_ff_2_q), .reset(or_1_out));  // open: Qn, preset
  D_Flip_Flop d_ff_3 (.D(d_ff_2_q), .clk(clk_256_out), .Q(d_ff_3_q), .reset(or_1_out));  // open: Qn, preset
  xor xor_1 (HP_S2_data_ready, d_ff_2_q, d_ff_3_q);
endmodule

module KEYPAD_state_3 (
  input  s3,
  input  RESET,
  output timer_out
);

  wire clk_256_out, not_1_out, or_1_out;

  Clock sysclk ();  // open: out
  Clock #(.highDuration(10), .lowDuration(10)) clk_256 (.out(clk_256_out));
  not not_1 (not_1_out, s3);
  or or_1 (or_1_out, not_1_out, RESET);
  Counter counter_1 (.clr(or_1_out), .clk(clk_256_out), .carry(timer_out));  // open: load, up, count, D, Q
endmodule

module KEYPAD_bubble (
  input  Input_1,
  input  x2,
  input  Input_2,
  input  Input_3,
  output X1,
  output Output_1,
  output X3,
  output X4
);

  wire and_1_out, and_2_out, and_3_out, not_1_out, not_2_out, not_3_out;

  not not_1 (not_1_out, Input_1);
  not not_2 (not_2_out, x2);
  not not_3 (not_3_out, Input_2);
  and and_1 (and_1_out, not_1_out, x2);
  and and_2 (and_2_out, Input_1, not_2_out);
  and and_3 (and_3_out, Input_1, not_3_out);
  or or_1 (X1, and_1_out, and_2_out, and_3_out);

  assign Output_1 = Input_1;
  assign X3 = x2;
  assign X4 = Input_2;
endmodule

module KEYPAD_bubble_counter (
  input  R,
  input  S,
  input  clk,
  output colddriver0,
  output colddriver1,
  output colddriver2,
  output colddriver3
);

  wire keypad_bubble_1_output_1, keypad_bubble_1_x1, keypad_bubble_1_x3, keypad_bubble_1_x4;

  KEYPAD_bubble keypad_bubble_1 (
    .Input_1(colddriver0), .x2(colddriver1), .Input_2(colddriver2), .Input_3(colddriver3),
    .X1(keypad_bubble_1_x1), .Output_1(keypad_bubble_1_output_1), .X3(keypad_bubble_1_x3),
    .X4(keypad_bubble_1_x4));
  D_Flip_Flop d_ff_1 (.D(keypad_bubble_1_x1), .clk(clk), .Q(colddriver0), .preset(S), .reset(R));  // open: Qn
  D_Flip_Flop d_ff_2 (.D(keypad_bubble_1_output_1), .clk(clk), .Q(colddriver1), .preset(S), .reset(R));  // open: Qn
  D_Flip_Flop d_ff_3 (.D(keypad_bubble_1_x3), .clk(clk), .Q(colddriver2), .preset(S), .reset(R));  // open: Qn
  D_Flip_Flop d_ff_4 (.D(keypad_bubble_1_x4), .clk(clk), .Q(colddriver3), .preset(S), .reset(R));  // open: Qn
endmodule

module KEYPAD_three_level_digfilter (
  input  button_in,
  input  RESET,
  output Output_1
);

  wire and_1_out, and_2_out, clk_256_out, d_ff_1_q, d_ff_2_q, d_ff_3_q, d_ff_4_q;

  Clock sysclk ();  // open: out
  Clock clk_256 (.out(clk_256_out));
  D_Flip_Flop d_ff_1 (.D(button_in), .clk(clk_256_out), .Q(d_ff_1_q), .reset(RESET));  // open: Qn, preset
  D_Flip_Flop d_ff_2 (.D(d_ff_1_q), .clk(clk_256_out), .Q(d_ff_2_q), .reset(RESET));  // open: Qn, preset
  D_Flip_Flop d_ff_3 (.D(d_ff_2_q), .clk(clk_256_out), .Q(d_ff_3_q), .reset(RESET));  // open: Qn, preset
  D_Flip_Flop d_ff_4 (.D(d_ff_3_q), .clk(clk_256_out), .Q(d_ff_4_q), .reset(RESET));  // open: Qn, preset
  and and_1 (and_1_out, d_ff_2_q, d_ff_3_q, d_ff_4_q);
  and and_2 (and_2_out, ~d_ff_4_q, ~d_ff_3_q, ~d_ff_2_q);  // AND_Gate
  J_K_Flip_Flop j_k_ff_1 (.J(and_1_out), .K(and_2_out), .clk(clk_256_out), .Q(Output_1));  // open: Qn, preset, reset
endmodule

module KEYPAD_debounce_4 (
  input  ch0,
  input  ch1,
  input  ch2,
  input  ch3,
  input  RESET,
  output ch0_dout,
  output ch1_dout,
  output ch2_dout,
  output ch3_dout
);

  Clock sysclk ();  // open: out
  KEYPAD_three_level_digfilter keypad_three_level_digfilter_1 (.button_in(ch0), .RESET(RESET), .Output_1(ch0_dout));
  KEYPAD_three_level_digfilter keypad_three_level_digfilter_2 (.button_in(ch1), .RESET(RESET), .Output_1(ch1_dout));
  KEYPAD_three_level_digfilter keypad_three_level_digfilter_3 (.button_in(ch2), .RESET(RESET), .Output_1(ch2_dout));
  KEYPAD_three_level_digfilter keypad_three_level_digfilter_4 (.button_in(ch3), .RESET(RESET), .Output_1(ch3_dout));
endmodule

module KEYPAD_register_8bit (
  input  clk01,
  input  clk02,
  input  RESET,
  input  b0,
  input  b1,
  input  b2,
  input  b3,
  input  b4,
  input  b5,
  input  b6,
  input  b7,
  output Output_1,
  output Output_2,
  output Output_3,
  output Output_4,
  output Output_5,
  output Output_6,
  output Output_7,
  output Output_8
);

  Clock sysclk ();  // open: out
  D_Flip_Flop d_ff_1 (.D(b0), .clk(clk01), .Q(Output_1), .preset(RESET));  // open: Qn, reset
  D_Flip_Flop d_ff_2 (.D(b1), .clk(clk01), .Q(Output_2), .reset(RESET));  // open: Qn, preset
  D_Flip_Flop d_ff_3 (.D(b2), .clk(clk01), .Q(Output_3), .reset(RESET));  // open: Qn, preset
  D_Flip_Flop d_ff_4 (.D(b3), .clk(clk01), .Q(Output_4), .reset(RESET));  // open: Qn, preset
  D_Flip_Flop d_ff_5 (.D(b4), .clk(clk02), .Q(Output_5), .reset(RESET));  // open: Qn, preset
  D_Flip_Flop d_ff_6 (.D(b5), .clk(clk02), .Q(Output_6), .reset(RESET));  // open: Qn, preset
  D_Flip_Flop d_ff_7 (.D(b6), .clk(clk02), .Q(Output_7), .reset(RESET));  // open: Qn, preset
  D_Flip_Flop d_ff_8 (.D(b7), .clk(clk02), .Q(Output_8), .reset(RESET));  // open: Qn, preset
endmodule

module KEYPAD_decodeur (
  input  Y1,
  input  Y2,
  input  Y3,
  input  Y4,
  input  Input_1,
  input  Input_2,
  input  Input_3,
  input  X4,
  output x0,
  output x1,
  output x2,
  output x3
);

  wire and_1_out, and_2_out, and_3_out, and_4_out, and_5_out, and_6_out, and_7_out, and_8_out, and_9_out,
       and_10_out, and_11_out, and_12_out, and_13_out, and_14_out, and_15_out, and_16_out, and_17_out,
       and_18_out, and_19_out, and_20_out, and_21_out, and_22_out, and_23_out, and_24_out, and_25_out,
       and_26_out, and_27_out, and_28_out, and_29_out, and_30_out, and_31_out, and_32_out, and_33_out,
       and_34_out, and_35_out, and_36_out, and_37_out, and_38_out, and_39_out, and_40_out, and_41_out,
       and_42_out, and_43_out, and_44_out, and_45_out, and_46_out, and_47_out, and_48_out, and_49_out,
       and_50_out, and_51_out, and_52_out, and_53_out, and_54_out, and_55_out, and_56_out, and_57_out,
       and_58_out, and_59_out, and_60_out, and_61_out, and_62_out, not_1_out, not_2_out, not_3_out,
       not_4_out, not_5_out, not_6_out, not_7_out, not_8_out;

  not not_1 (not_1_out, Y1);
  not not_2 (not_2_out, Y2);
  not not_3 (not_3_out, Y3);
  not not_4 (not_4_out, Y4);
  not not_5 (not_5_out, Input_1);
  not not_6 (not_6_out, Input_2);
  not not_7 (not_7_out, Input_3);
  not not_8 (not_8_out, X4);
  and and_1 (and_1_out, not_2_out, not_3_out, not_4_out);
  and and_2 (and_2_out, not_3_out, not_6_out, not_7_out, not_8_out);
  and and_3 (and_3_out, not_4_out, not_5_out, not_7_out, not_8_out);
  and and_4 (and_4_out, Input_3, X4);
  and and_5 (and_5_out, not_4_out, Input_2);
  and and_6 (and_6_out, Input_2, X4);
  and and_7 (and_7_out, Input_2, Input_3);
  and and_8 (and_8_out, not_3_out, Input_1);
  and and_9 (and_9_out, Input_1, X4);
  and and_10 (and_10_out, Input_1, Input_3);
  and and_11 (and_11_out, Y3, Y4);
  and and_12 (and_12_out, Y2, Y4);
  and and_13 (and_13_out, Y2, Y3);
  and and_14 (and_14_out, not_1_out, not_2_out, not_3_out, not_4_out);
  and and_15 (and_15_out, not_3_out, not_6_out, not_7_out, not_8_out);
  and and_16 (and_16_out, not_5_out, not_6_out, not_7_out, not_8_out);
  and and_17 (and_17_out, not_1_out, Input_3);
  and and_18 (and_18_out, Input_3, X4);
  and and_19 (and_19_out, not_2_out, not_3_out, Input_2);
  and and_20 (and_20_out, Input_2, X4);
  and and_21 (and_21_out, not_3_out, Input_1);
  and and_22 (and_22_out, Input_1, X4);
  and and_23 (and_23_out, Input_1, Input_2);
  and and_24 (and_24_out, Y3, Y4);
  and and_25 (and_25_out, Y2, Y4);
  and and_26 (and_26_out, Y2, Y3);
  and and_27 (and_27_out, Y1, Y4);
  and and_28 (and_28_out, Y1, Y3);
  and and_29 (and_29_out, Y1, Y2);
  and and_30 (and_30_out, not_1_out, not_2_out, not_3_out, not_4_out);
  and and_31 (and_31_out, not_3_out, not_4_out, not_5_out, not_6_out);
  and and_32 (and_32_out, not_4_out, not_5_out, not_6_out, not_7_out);
  and and_33 (and_33_out, not_4_out, X4);
  and and_34 (and_34_out, Input_3, X4);
  and and_35 (and_35_out, Input_2, Input_3);
  and and_36 (and_36_out, not_1_out, not_3_out, Input_1);
  and and_37 (and_37_out, Input_1, Input_3);
  and and_38 (and_38_out, Input_1, Input_2);
  and and_39 (and_39_out, Y4, not_7_out, not_8_out);
  and and_40 (and_40_out, Y4, Input_2);
  and and_41 (and_41_out, Y3, Y4);
  and and_42 (and_42_out, Y2, not_6_out);
  and and_43 (and_43_out, Y2, Y3);
  and and_44 (and_44_out, Y1, Y4);
  and and_45 (and_45_out, Y1, Y3);
  and and_46 (and_46_out, Y1, Y2);
  and and_47 (and_47_out, not_1_out, not_2_out, not_3_out, not_4_out);
  and and_48 (and_48_out, not_5_out, not_6_out, not_7_out, not_8_out);
  and and_49 (and_49_out, Input_3, X4);
  and and_50 (and_50_out, Input_2, X4);
  and and_51 (and_51_out, Input_2, Input_3);
  and and_52 (and_52_out, Input_1, X4);
  and and_53 (and_53_out, Input_1, Input_3);
  and and_54 (and_54_out, Input_1, Input_2);
  and and_55 (and_55_out, Y4, not_7_out);
  and and_56 (and_56_out, Y3, Input_3);
  and and_57 (and_57_out, Y2, not_5_out, not_7_out);
  and and_58 (and_58_out, Y2, Y4);
  and and_59 (and_59_out, Y2, Y3);
  and and_60 (and_60_out, Y1, not_6_out, not_8_out);
  and and_61 (and_61_out, Y1, Input_3);
  and and_62 (and_62_out, Y1, Y3);
  or or_1 (x3, and_1_out, and_2_out, and_3_out, and_4_out, and_5_out, and_6_out, and_7_out, and_8_out, and_9_out, and_10_out, and_11_out, and_12_out, and_13_out, Y1);
  or or_2 (x2, and_14_out, and_15_out, and_16_out, and_17_out, and_18_out, and_19_out, and_20_out, and_21_out, and_22_out, and_23_out, and_24_out, and_25_out, and_26_out, and_27_out, and_28_out, and_29_out);
  or or_3 (x1, and_30_out, and_31_out, and_32_out, and_33_out, and_34_out, and_35_out, and_36_out, and_37_out, and_38_out, and_39_out, and_40_out, and_41_out, and_42_out, and_43_out, and_44_out, and_45_out, and_46_out);
  or or_4 (x0, and_47_out, and_48_out, and_49_out, and_50_out, and_51_out, and_52_out, and_53_out, and_54_out, and_55_out, and_56_out, and_57_out, and_58_out, and_59_out, and_60_out, and_61_out, and_62_out);
endmodule

module digit_8 (
  input  X0,
  input  X1,
  input  X2,
  input  X3,
  input  Y,
  output a,
  output b,
  output c,
  output d,
  output e,
  output f,
  output g,
  output DOT
);

  wire and_1_out, and_2_out, and_3_out, and_4_out, and_5_out, and_6_out, and_7_out, and_8_out, and_9_out,
       and_10_out, and_11_out, and_12_out, and_13_out, and_14_out, and_15_out, and_16_out, and_17_out,
       and_18_out, and_19_out, and_20_out, and_21_out, and_22_out, and_23_out, and_24_out, and_25_out,
       and_26_out, and_27_out, and_28_out, and_29_out, and_30_out, and_31_out, and_32_out, not_1_out,
       not_2_out, not_3_out, not_4_out;

  not not_1 (not_1_out, X0);
  not not_2 (not_2_out, X1);
  not not_3 (not_3_out, X2);
  not not_4 (not_4_out, X3);
  and and_1 (and_1_out, not_1_out, not_3_out);
  and and_2 (and_2_out, not_1_out, not_2_out, X3);
  and and_3 (and_3_out, not_2_out, not_3_out, X3);
  and and_4 (and_4_out, X1, not_4_out);
  and and_5 (and_5_out, X0, X2, not_4_out);
  and and_6 (and_6_out, not_1_out, not_2_out, not_4_out);
  and and_7 (and_7_out, not_2_out, not_3_out);
  and and_8 (and_8_out, not_3_out, not_4_out);
  and and_9 (and_9_out, not_1_out, X1, X3);
  and and_10 (and_10_out, X0, not_2_out, X3);
  and and_11 (and_11_out, X0, X1, not_4_out);
  and and_12 (and_12_out, not_2_out, not_3_out);
  and and_13 (and_13_out, not_3_out, X3);
  and and_14 (and_14_out, X2, not_4_out);
  and and_15 (and_15_out, X0, not_2_out);
  and and_16 (and_16_out, X0, not_3_out);
  and and_17 (and_17_out, not_1_out, not_2_out, not_3_out);
  and and_18 (and_18_out, not_2_out, X3);
  and and_19 (and_19_out, not_1_out, X1, not_4_out);
  and and_20 (and_20_out, X0, not_2_out, X2);
  and and_21 (and_21_out, X0, X1, not_3_out);
  and and_22 (and_22_out, not_1_out, not_3_out);
  and and_23 (and_23_out, not_2_out, X2, X3);
  and and_24 (and_24_out, not_1_out, X1);
  and and_25 (and_25_out, X1, not_3_out, X3);
  and and_26 (and_26_out, not_1_out, not_2_out);
  and and_27 (and_27_out, not_3_out, X3);
  and and_28 (and_28_out, not_1_out, X2, not_4_out);
  and and_29 (and_29_out, not_2_out, X2, not_4_out);
  and and_30 (and_30_out, X3, X2, not_2_out, not_1_out);
  and and_31 (and_31_out, not_4_out, X2, X1, X0);
  and and_32 (and_32_out, not_4_out, not_3_out, not_2_out);
  or or_1 (a, and_1_out, and_2_out, and_3_out, and_4_out, and_5_out);
  or or_2 (b, and_6_out, and_7_out, and_8_out, and_9_out, and_10_out, and_11_out);
  or or_3 (c, and_12_out, and_13_out, and_14_out, and_15_out, and_16_out);
  or or_4 (d, and_17_out, and_18_out, and_19_out, and_20_out, and_21_out);
  or or_5 (e, and_22_out, and_23_out, and_24_out, and_25_out);
  or or_6 (f, and_26_out, and_27_out, and_28_out, and_29_out);
  nor nor_1 (g, and_30_out, and_31_out, and_32_out);

  assign DOT = Y;
endmodule

module count_3 (
  input  Q1,
  input  Q0,
  output U1,
  output U0,
  output CO
);

  wire not_1_out, not_2_out, not_3_out, not_4_out;

  not not_1 (not_1_out, Q1);
  not not_2 (not_2_out, Q1);
  not not_3 (not_3_out, Q0);
  not not_4 (not_4_out, Q0);
  and and_1 (U1, not_1_out, Q0);
  and and_2 (U0, not_2_out, not_3_out);
  and and_3 (CO, Q1, not_4_out);
endmodule

module count_6 (
  input  Q2,
  input  Q1,
  input  Q0,
  output U2,
  output U1,
  output U0,
  output CO
);

  wire and_1_out, and_2_out, and_3_out, and_4_out, and_5_out, and_6_out, not_1_out, not_2_out, not_3_out,
       not_4_out, not_5_out, not_6_out, not_7_out, not_8_out, not_9_out, not_10_out, not_11_out, not_12_out;

  not not_1 (not_1_out, Q2);
  not not_2 (not_2_out, Q1);
  not not_3 (not_3_out, Q0);
  not not_4 (not_4_out, Q2);
  not not_5 (not_5_out, Q1);
  not not_6 (not_6_out, Q2);
  not not_7 (not_7_out, Q0);
  not not_8 (not_8_out, Q2);
  not not_9 (not_9_out, Q0);
  not not_10 (not_10_out, Q1);
  not not_11 (not_11_out, Q0);
  not not_12 (not_12_out, Q1);
  and and_1 (and_1_out, not_1_out, Q1, Q0);
  and and_2 (and_2_out, Q2, not_2_out, not_3_out);
  and and_3 (and_3_out, not_4_out, not_5_out, Q0);
  and and_4 (and_4_out, not_6_out, Q1, not_7_out);
  and and_5 (and_5_out, not_8_out, not_9_out);
  and and_6 (and_6_out, not_10_out, not_11_out);
  and and_7 (CO, Q2, not_12_out, Q0);
  or or_1 (U2, and_1_out, and_2_out);
  or or_2 (U1, and_3_out, and_4_out);
  or or_3 (U0, and_5_out, and_6_out);
endmodule

module count_10 (
  input  Q3,
  input  Q2,
  input  Q1,
  input  Q0,
  output U3,
  output U2,
  output U1,
  output U0,
  output CO
);

  wire and_1_out, and_2_out, and_3_out, and_4_out, and_5_out, and_6_out, and_7_out, and_8_out, and_9_out,
       not_1_out, not_2_out, not_3_out, not_4_out;

  not not_1 (not_1_out, Q3);
  not not_2 (not_2_out, Q2);
  not not_3 (not_3_out, Q1);
  not not_4 (not_4_out, Q0);
  and and_1 (and_1_out, not_1_out, Q2, Q1, Q0);
  and and_2 (and_2_out, Q3, not_2_out, not_3_out, not_4_out);
  and and_3 (and_3_out, not_1_out, not_2_out, Q1, Q0);
  and and_4 (and_4_out, not_1_out, Q2, not_3_out);
  and and_5 (and_5_out, not_1_out, Q2, not_4_out);
  and and_6 (and_6_out, not_1_out, not_3_out, Q0);
  and and_7 (and_7_out, not_1_out, Q1, not_4_out);
  and and_8 (and_8_out, not_1_out, not_4_out);
  and and_9 (and_9_out, not_2_out, not_3_out, not_4_out);
  and and_10 (CO, Q3, not_2_out, not_3_out, Q0);
  or or_1 (U3, and_1_out, and_2_out);
  or or_2 (U2, and_3_out, and_4_out, and_5_out);
  or or_3 (U1, and_6_out, and_7_out);
  or or_4 (U0, and_8_out, and_9_out);
endmodule

module count_10_4 (
  input  H,
  input  Q3,
  input  Q2,
  input  Q1,
  input  Q0,
  output U3,
  output U2,
  output U1,
  output U0,
  output CO
);

  wire and_1_out, and_2_out, and_3_out, and_4_out, and_5_out, and_6_out, and_7_out, and_8_out, and_9_out,
       and_10_out, and_11_out, and_12_out, and_13_out, and_14_out, not_1_out, not_2_out, not_3_out,
       not_4_out, not_5_out;

  not not_1 (not_1_out, H);
  not not_2 (not_2_out, Q3);
  not not_3 (not_3_out, Q2);
  not not_4 (not_4_out, Q1);
  not not_5 (not_5_out, Q0);
  and and_1 (and_1_out, not_1_out, not_2_out, Q2, Q1, Q0);
  and and_2 (and_2_out, not_1_out, Q3, not_3_out, not_4_out, not_5_out);
  and and_3 (and_3_out, not_1_out, not_2_out, not_3_out, Q1, Q0);
  and and_4 (and_4_out, not_1_out, not_2_out, Q2, not_4_out);
  and and_5 (and_5_out, not_1_out, not_2_out, Q2, not_5_out);
  and and_6 (and_6_out, not_1_out, not_2_out, not_4_out, Q0);
  and and_7 (and_7_out, not_2_out, not_3_out, not_4_out, Q0);
  and and_8 (and_8_out, not_1_out, not_2_out, Q1, not_5_out);
  and and_9 (and_9_out, not_2_out, not_3_out, Q1, not_5_out);
  and and_10 (and_10_out, not_1_out, not_2_out, not_5_out);
  and and_11 (and_11_out, not_1_out, not_3_out, not_4_out, not_5_out);
  and and_12 (and_12_out, not_2_out, not_3_out, not_5_out);
  and and_13 (and_13_out, not_1_out, Q3, not_3_out, not_4_out, Q0);
  and and_14 (and_14_out, H, not_2_out, not_3_out, Q1, Q0);
  or or_1 (U3, and_1_out, and_2_out);
  or or_2 (U2, and_3_out, and_4_out, and_5_out);
  or or_3 (U1, and_6_out, and_7_out, and_8_out, and_9_out);
  or or_4 (U0, and_10_out, and_11_out, and_12_out);
  or or_5 (CO, and_13_out, and_14_out);
endmodule

module count_rev_3 (
  input  Q1,
  input  Q0,
  output U1,
  output U0,
  output CO
);

  wire not_1_out, not_2_out;

  not not_1 (not_1_out, Q1);
  not not_2 (not_2_out, Q0);
  and and_1 (U1, not_1_out, not_2_out);
  and and_2 (U0, Q1, not_2_out);
  and and_3 (CO, not_1_out, not_2_out);
endmodule

module count_rev_6 (
  input  Q2,
  input  Q1,
  input  Q0,
  output U2,
  output U1,
  output U0,
  output CO
);

  wire and_1_out, and_2_out, and_3_out, and_4_out, and_5_out, and_6_out, not_1_out, not_2_out, not_3_out;

  not not_1 (not_1_out, Q2);
  not not_2 (not_2_out, Q1);
  not not_3 (not_3_out, Q0);
  and and_1 (and_1_out, not_1_out, not_2_out, not_3_out);
  and and_2 (and_2_out, Q2, not_2_out, Q0);
  and and_3 (and_3_out, not_1_out, Q1, Q0);
  and and_4 (and_4_out, Q2, not_2_out, not_3_out);
  and and_5 (and_5_out, not_1_out, not_3_out);
  and and_6 (and_6_out, not_2_out, not_3_out);
  and and_7 (CO, not_1_out, not_2_out, not_3_out);
  or or_1 (U2, and_1_out, and_2_out);
  or or_2 (U1, and_3_out, and_4_out);
  or or_3 (U0, and_5_out, and_6_out);
endmodule

module count_rev_10 (
  input  Q3,
  input  Q2,
  input  Q1,
  input  Q0,
  output U3,
  output U2,
  output U1,
  output U0,
  output CO
);

  wire and_1_out, and_2_out, and_3_out, and_4_out, and_5_out, and_6_out, and_7_out, and_8_out, and_9_out,
       and_10_out, not_1_out, not_2_out, not_3_out, not_4_out;

  not not_1 (not_1_out, Q3);
  not not_2 (not_2_out, Q2);
  not not_3 (not_3_out, Q1);
  not not_4 (not_4_out, Q0);
  and and_1 (and_1_out, not_1_out, not_2_out, not_3_out, not_4_out);
  and and_2 (and_2_out, Q3, not_2_out, not_3_out, Q0);
  and and_3 (and_3_out, not_1_out, Q2, Q0);
  and and_4 (and_4_out, not_1_out, Q2, Q1);
  and and_5 (and_5_out, Q3, not_2_out, not_3_out, not_4_out);
  and and_6 (and_6_out, not_1_out, Q1, Q0);
  and and_7 (and_7_out, not_1_out, Q2, not_3_out, not_4_out);
  and and_8 (and_8_out, Q3, not_2_out, not_3_out, not_4_out);
  and and_9 (and_9_out, not_1_out, not_4_out);
  and and_10 (and_10_out, not_2_out, not_3_out, not_4_out);
  and and_11 (CO, not_1_out, not_2_out, not_3_out, not_4_out);
  or or_1 (U3, and_1_out, and_2_out);
  or or_2 (U2, and_3_out, and_4_out, and_5_out);
  or or_3 (U1, and_6_out, and_7_out, and_8_out);
  or or_4 (U0, and_9_out, and_10_out);
endmodule

module count_rev_10_4 (
  input  H1,
  input  H0,
  input  Q3,
  input  Q2,
  input  Q1,
  input  Q0,
  output U3,
  output U2,
  output U1,
  output U0,
  output CO
);

  wire and_1_out, and_2_out, and_3_out, and_4_out, and_5_out, and_6_out, and_7_out, and_8_out, and_9_out,
       and_10_out, and_11_out, and_12_out, not_1_out, not_2_out, not_3_out, not_4_out, not_5_out, not_6_out;

  not not_1 (not_1_out, H1);
  not not_2 (not_2_out, H0);
  not not_3 (not_3_out, Q3);
  not not_4 (not_4_out, Q2);
  not not_5 (not_5_out, Q1);
  not not_6 (not_6_out, Q0);
  and and_1 (and_1_out, Q3, not_4_out, not_5_out, Q0);
  and and_2 (and_2_out, H0, not_3_out, not_4_out, not_5_out, not_6_out);
  and and_3 (and_3_out, H1, not_3_out, not_4_out, not_5_out, not_6_out);
  and and_4 (and_4_out, not_3_out, Q2, Q0);
  and and_5 (and_5_out, not_3_out, Q2, Q1);
  and and_6 (and_6_out, Q3, not_4_out, not_5_out, not_6_out);
  and and_7 (and_7_out, not_1_out, not_2_out, not_3_out, not_5_out, not_6_out);
  and and_8 (and_8_out, not_3_out, Q1, Q0);
  and and_9 (and_9_out, not_3_out, Q2, not_5_out, not_6_out);
  and and_10 (and_10_out, Q3, not_4_out, not_5_out, not_6_out);
  and and_11 (and_11_out, not_3_out, not_6_out);
  and and_12 (and_12_out, not_4_out, not_5_out, not_6_out);
  and and_13 (CO, not_3_out, not_4_out, not_5_out, not_6_out);
  or or_1 (U3, and_1_out, and_2_out, and_3_out);
  or or_2 (U2, and_4_out, and_5_out, and_6_out);
  or or_3 (U1, and_7_out, and_8_out, and_9_out, and_10_out);
  or or_4 (U0, and_11_out, and_12_out);
endmodule

module shift_register (
  input  N0,
  input  N1,
  input  N2,
  input  N3,
  input  clock,
  input  R,
  output [29:0] SET_TIME
);

  D_Flip_Flop d_ff_1 (.D(N0), .clk(clock), .Q(SET_TIME[0]), .preset(R));  // open: Qn, reset
  D_Flip_Flop d_ff_2 (.D(N1), .clk(clock), .Q(SET_TIME[1]), .preset(R));  // open: Qn, reset
  D_Flip_Flop d_ff_3 (.D(N2), .clk(clock), .Q(SET_TIME[2]), .preset(R));  // open: Qn, reset
  D_Flip_Flop d_ff_4 (.D(N3), .clk(clock), .Q(SET_TIME[3]), .preset(R));  // open: Qn, reset
  D_Flip_Flop d_ff_5 (.D(SET_TIME[0]), .clk(clock), .Q(SET_TIME[5]), .preset(R));  // open: Qn, reset
  D_Flip_Flop d_ff_6 (.D(SET_TIME[1]), .clk(clock), .Q(SET_TIME[6]), .preset(R));  // open: Qn, reset
  D_Flip_Flop d_ff_7 (.D(SET_TIME[2]), .clk(clock), .Q(SET_TIME[7]), .preset(R));  // open: Qn, reset
  D_Flip_Flop d_ff_8 (.D(SET_TIME[3]), .clk(clock), .Q(SET_TIME[8]), .preset(R));  // open: Qn, reset
  D_Flip_Flop d_ff_9 (.D(SET_TIME[5]), .clk(clock), .Q(SET_TIME[10]), .preset(R));  // open: Qn, reset
  D_Flip_Flop d_ff_10 (.D(SET_TIME[6]), .clk(clock), .Q(SET_TIME[11]), .preset(R));  // open: Qn, reset
  D_Flip_Flop d_ff_11 (.D(SET_TIME[7]), .clk(clock), .Q(SET_TIME[12]), .preset(R));  // open: Qn, reset
  D_Flip_Flop d_ff_12 (.D(SET_TIME[8]), .clk(clock), .Q(SET_TIME[13]), .preset(R));  // open: Qn, reset
  D_Flip_Flop d_ff_13 (.D(SET_TIME[10]), .clk(clock), .Q(SET_TIME[15]), .preset(R));  // open: Qn, reset
  D_Flip_Flop d_ff_14 (.D(SET_TIME[11]), .clk(clock), .Q(SET_TIME[16]), .preset(R));  // open: Qn, reset
  D_Flip_Flop d_ff_15 (.D(SET_TIME[12]), .clk(clock), .Q(SET_TIME[17]), .preset(R));  // open: Qn, reset
  D_Flip_Flop d_ff_16 (.D(SET_TIME[13]), .clk(clock), .Q(SET_TIME[18]), .preset(R));  // open: Qn, reset
  D_Flip_Flop d_ff_17 (.D(SET_TIME[15]), .clk(clock), .Q(SET_TIME[20]), .preset(R));  // open: Qn, reset
  D_Flip_Flop d_ff_18 (.D(SET_TIME[16]), .clk(clock), .Q(SET_TIME[21]), .preset(R));  // open: Qn, reset
  D_Flip_Flop d_ff_19 (.D(SET_TIME[17]), .clk(clock), .Q(SET_TIME[22]), .preset(R));  // open: Qn, reset
  D_Flip_Flop d_ff_20 (.D(SET_TIME[18]), .clk(clock), .Q(SET_TIME[23]), .preset(R));  // open: Qn, reset
  D_Flip_Flop d_ff_21 (.D(SET_TIME[20]), .clk(clock), .Q(SET_TIME[25]), .preset(R));  // open: Qn, reset
  D_Flip_Flop d_ff_22 (.D(SET_TIME[21]), .clk(clock), .Q(SET_TIME[26]), .preset(R));  // open: Qn, reset
  D_Flip_Flop d_ff_23 (.D(SET_TIME[22]), .clk(clock), .Q(SET_TIME[27]), .preset(R));  // open: Qn, reset
  D_Flip_Flop d_ff_24 (.D(SET_TIME[23]), .clk(clock), .Q(SET_TIME[28]), .preset(R));  // open: Qn, reset

  assign {SET_TIME[29], SET_TIME[24], SET_TIME[19], SET_TIME[14], SET_TIME[9], SET_TIME[4]} = 6'b010101;
endmodule

module long_press (
  input  in_1,
  output out_2
);

  wire d_ff_1_q, d_ff_2_q, d_ff_3_q, SECONDES_out;

  Clock #(.highDuration(8000), .lowDuration(8000)) SECONDES (.out(SECONDES_out));
  D_Flip_Flop d_ff_1 (.D(in_1), .clk(SECONDES_out), .Q(d_ff_1_q));  // open: Qn, preset, reset
  D_Flip_Flop d_ff_2 (.D(d_ff_1_q), .clk(SECONDES_out), .Q(d_ff_2_q));  // open: Qn, preset, reset
  D_Flip_Flop d_ff_3 (.D(d_ff_2_q), .clk(SECONDES_out), .Q(d_ff_3_q));  // open: Qn, preset, reset
  and and_1 (out_2, d_ff_1_q, d_ff_2_q, d_ff_3_q);
endmodule

module longlong_press (
  input  in_1,
  output out_2
);

  wire d_ff_1_q, d_ff_2_q, d_ff_3_q, d_ff_4_q, d_ff_5_q, d_ff_6_q, SECONDES_out;

  Clock #(.highDuration(8000), .lowDuration(8000)) SECONDES (.out(SECONDES_out));
  D_Flip_Flop d_ff_1 (.D(in_1), .clk(SECONDES_out), .Q(d_ff_1_q));  // open: Qn, preset, reset
  D_Flip_Flop d_ff_2 (.D(d_ff_1_q), .clk(SECONDES_out), .Q(d_ff_2_q));  // open: Qn, preset, reset
  D_Flip_Flop d_ff_3 (.D(d_ff_2_q), .clk(SECONDES_out), .Q(d_ff_3_q));  // open: Qn, preset, reset
  D_Flip_Flop d_ff_4 (.D(d_ff_3_q), .clk(SECONDES_out), .Q(d_ff_4_q));  // open: Qn, preset, reset
  D_Flip_Flop d_ff_5 (.D(d_ff_4_q), .clk(SECONDES_out), .Q(d_ff_5_q));  // open: Qn, preset, reset
  D_Flip_Flop d_ff_6 (.D(d_ff_5_q), .clk(SECONDES_out), .Q(d_ff_6_q));  // open: Qn, preset, reset
  and and_1 (out_2, d_ff_1_q, d_ff_2_q, d_ff_3_q, d_ff_4_q, d_ff_6_q);
endmodule

module affichage_reset (
  output [29:0] out_1
);


  assign out_1 = 30'h1ce739ce;
endmodule

module affichage_reverse1 (
  input  [47:0] in_1,
  output [47:0] out_2
);

  affichage_reverse2 affichage_reverse2_1 (
    .a1(in_1[0]), .b1(in_1[1]), .c1(in_1[2]), .d1(in_1[3]), .e1(in_1[4]), .f1(in_1[5]), .g1(in_1[6]),
    .dot1(in_1[7]), .a2(out_2[40]), .b2(out_2[41]), .c2(out_2[42]), .d2(out_2[43]), .e2(out_2[44]),
    .f2(out_2[45]), .g2(out_2[46]), .dot2(out_2[47]));
  affichage_reverse2 affichage_reverse2_2 (
    .a1(in_1[8]), .b1(in_1[9]), .c1(in_1[10]), .d1(in_1[11]), .e1(in_1[12]), .f1(in_1[13]), .g1(in_1[14]),
    .dot1(in_1[15]), .a2(out_2[32]), .b2(out_2[33]), .c2(out_2[34]), .d2(out_2[35]), .e2(out_2[36]),
    .f2(out_2[37]), .g2(out_2[38]), .dot2(out_2[39]));
  affichage_reverse2 affichage_reverse2_3 (
    .a1(in_1[16]), .b1(in_1[17]), .c1(in_1[18]), .d1(in_1[19]), .e1(in_1[20]), .f1(in_1[21]), .g1(in_1[22]),
    .dot1(in_1[23]), .a2(out_2[24]), .b2(out_2[25]), .c2(out_2[26]), .d2(out_2[27]), .e2(out_2[28]),
    .f2(out_2[29]), .g2(out_2[30]), .dot2(out_2[31]));
  affichage_reverse2 affichage_reverse2_4 (
    .a1(in_1[24]), .b1(in_1[25]), .c1(in_1[26]), .d1(in_1[27]), .e1(in_1[28]), .f1(in_1[29]), .g1(in_1[30]),
    .dot1(in_1[31]), .a2(out_2[16]), .b2(out_2[17]), .c2(out_2[18]), .d2(out_2[19]), .e2(out_2[20]),
    .f2(out_2[21]), .g2(out_2[22]), .dot2(out_2[23]));
  affichage_reverse2 affichage_reverse2_5 (
    .a1(in_1[32]), .b1(in_1[33]), .c1(in_1[34]), .d1(in_1[35]), .e1(in_1[36]), .f1(in_1[37]), .g1(in_1[38]),
    .dot1(in_1[39]), .a2(out_2[8]), .b2(out_2[9]), .c2(out_2[10]), .d2(out_2[11]), .e2(out_2[12]),
    .f2(out_2[13]), .g2(out_2[14]), .dot2(out_2[15]));
  affichage_reverse2 affichage_reverse2_6 (
    .a1(in_1[40]), .b1(in_1[41]), .c1(in_1[42]), .d1(in_1[43]), .e1(in_1[44]), .f1(in_1[45]), .g1(in_1[46]),
    .a2(out_2[0]), .b2(out_2[1]), .c2(out_2[2]), .d2(out_2[3]), .e2(out_2[4]), .f2(out_2[5]), .g2(out_2[6]),
    .dot2(out_2[7]));  // open: dot1
endmodule

module affichage_reverse2 (
  input  a1,
  input  b1,
  input  c1,
  input  d1,
  input  e1,
  input  f1,
  input  g1,
  input  dot1,
  output a2,
  output b2,
  output c2,
  output d2,
  output e2,
  output f2,
  output g2,
  output dot2
);

  not not_1 (dot2, dot1);

  assign a2 = d1;
  assign b2 = e1;
  assign c2 = f1;
  assign d2 = a1;
  assign e2 = b1;
  assign f2 = c1;
  assign g2 = g1;

  // Notes on the sheet:
  //   e
endmodule
